// Logisim project adders.circ as structural Verilog
module FA0 (
  input  a,
  input  b,
  output s,
  output cout
);

  wire nor_1_out;

  and and_1 (cout, a, b);
  nor nor_1 (nor_1_out, a, b);
  nor nor_2 (s, nor_1_out, cout);

  // Notes on the sheet:
  //   14 transistors
  //   FA0
  //   Seth Mueller
  //   2.75
  //   1.75
endmodule

module FA1 (
  input  a,
  input  b,
  output cout,
  output s
);

  wire nand_1_out;

  or or_1 (cout, a, b);
  nand nand_1 (nand_1_out, a, b);
  nand nand_2 (s, cout, nand_1_out);

  // Notes on the sheet:
  //   14 transistors
  //   FA1
  //   Seth Mueller
  //   1.75
  //   2.75
endmodule

module FAopt1 (
  input  a,
  input  b,
  input  cin,
  output s,
  output cout
);

  wire nand_1_out, nand_2_out, nor_1_out, nor_2_out, nor_3_out, not_1_out, not_2_out;

  nand nand_1 (nand_1_out, a, b);
  nor nor_1 (nor_1_out, a, b);
  not not_1 (not_1_out, nand_1_out);
  nor nor_2 (nor_2_out, nor_1_out, not_1_out);
  nor nor_3 (nor_3_out, nor_2_out, cin);
  not not_2 (not_2_out, nand_2_out);
  nand nand_2 (nand_2_out, nor_2_out, cin);
  nor nor_4 (s, nor_3_out, not_2_out);
  nand nand_3 (cout, nand_2_out, nand_1_out);

  // Notes on the sheet:
  //   32 transistors
  //   FAopt1
  //   Seth Mueller
  //   120 Transisors
  //   5.5 if cin<2.75
  //   cin+2.75 if cin>2.75
  //   4.75 if cin<2.75
  //   cin+2 if cin>2.75
endmodule

module FAopt2 (
  input  a,
  input  b,
  input  cin,
  output s,
  output cout
);

  wire and_1_out, nand_1_out, nand_2_out, nand_3_out, nor_1_out, nor_2_out, nor_3_out, not_1_out;

  nor nor_1 (nor_1_out, a, b);
  nor nor_2 (nor_2_out, nor_1_out, not_1_out);
  not not_1 (not_1_out, nand_1_out);
  nand nand_1 (nand_1_out, a, b);
  nand nand_2 (nand_2_out, cin, b);
  nand nand_3 (nand_3_out, a, cin);
  nand nand_4 (cout, nand_1_out, nand_2_out, nand_3_out);
  nor nor_3 (nor_3_out, nor_2_out, cin);
  and and_1 (and_1_out, nor_2_out, cin);
  nor nor_4 (s, nor_3_out, and_1_out);

  // Notes on the sheet:
  //   42 transistors
  //   cin+2.25
  //   FAopt2
  //   Seth Mueller
  //   5.5 if cin<2.75
  //   cin+2.75 if cin>2.75
endmodule

module Ripple4bit (
  input  [3:0] a,
  input  [3:0] b,
  output [3:0] s,
  output cout
);

  wire fa0_1_cout, faopt1_2_cout, faopt2_1_cout;

  FAopt1 faopt1_1 (.a(a[3]), .b(b[3]), .cin(faopt1_2_cout), .s(s[3]), .cout(cout));
  FAopt1 faopt1_2 (.a(a[2]), .b(b[2]), .cin(faopt2_1_cout), .s(s[2]), .cout(faopt1_2_cout));
  FAopt2 faopt2_1 (.a(a[1]), .b(b[1]), .cin(fa0_1_cout), .s(s[1]), .cout(faopt2_1_cout));
  FA0 fa0_1 (.b(b[0]), .a(a[0]), .s(s[0]), .cout(fa0_1_cout));

  // Notes on the sheet:
  //   8
  //   6
  //   8.75
  //   4
  //   6.75
  //   8.75
  //   8
  //   1.75
  //   5.5
  //   2.75
  //   Ripple4bit
  //   Seth Mueller
  //   120 transitors
endmodule

module Ripple8bit (
  input  [7:0] a,
  input  [7:0] b,
  output [7:0] s,
  output cout
);

  wire fa0_1_cout, faopt1_2_cout, faopt1_3_cout, faopt1_4_cout, faopt1_5_cout, faopt1_6_cout, faopt2_1_cout;

  FAopt1 faopt1_1 (.a(a[7]), .b(b[7]), .cin(faopt1_2_cout), .s(s[7]), .cout(cout));
  FAopt1 faopt1_2 (.a(a[6]), .b(b[6]), .cin(faopt1_3_cout), .s(s[6]), .cout(faopt1_2_cout));
  FAopt1 faopt1_3 (.a(a[5]), .b(b[5]), .cin(faopt1_4_cout), .s(s[5]), .cout(faopt1_3_cout));
  FAopt1 faopt1_4 (.a(a[4]), .b(b[4]), .cin(faopt1_5_cout), .s(s[4]), .cout(faopt1_4_cout));
  FAopt1 faopt1_5 (.a(a[3]), .b(b[3]), .cin(faopt1_6_cout), .s(s[3]), .cout(faopt1_5_cout));
  FAopt1 faopt1_6 (.a(a[2]), .b(b[2]), .cin(faopt2_1_cout), .s(s[2]), .cout(faopt1_6_cout));
  FAopt2 faopt2_1 (.a(a[1]), .b(b[1]), .cin(fa0_1_cout), .s(s[1]), .cout(faopt2_1_cout));
  FA0 fa0_1 (.b(b[0]), .a(a[0]), .s(s[0]), .cout(fa0_1_cout));

  // Notes on the sheet:
  //   16
  //   16.75
  //   14
  //   12
  //   14.75
  //   10
  //   12.75
  //   10.75
  //   8
  //   6
  //   8.75
  //   4
  //   6.75
  //   1.75
  //   5.5
  //   2.75
  //   Ripple8bit
  //   Seth Mueller
  //   240 transistors
  //   16.75
  //   16
endmodule

module Mux2_1 (
  input  in0,
  input  s,
  input  in1,
  output z
);

  wire nand_1_out, nand_2_out, not_1_out;

  not not_1 (not_1_out, s);
  nand nand_1 (nand_1_out, in0, not_1_out);
  nand nand_2 (nand_2_out, in1, s);
  nand nand_3 (z, nand_1_out, nand_2_out);

  // Notes on the sheet:
  //   14 transistors
  //   Mux2_1
  //   Seth Mueller
  //   max(s+2.75, in0+2, in1+2)
endmodule

module Mux4_1 (
  input  d00,
  input  d01,
  input  d10,
  input  d11,
  input  S0,
  input  S1,
  output O
);

  wire mux2_1_1_z, mux2_1_2_z;

  Mux2_1 mux2_1_1 (.in0(d00), .s(S0), .in1(d01), .z(mux2_1_1_z));
  Mux2_1 mux2_1_2 (.in0(d10), .s(S0), .in1(d11), .z(mux2_1_2_z));
  Mux2_1 mux2_1_3 (.in0(mux2_1_1_z), .s(S1), .in1(mux2_1_2_z), .z(O));

  // Notes on the sheet:
  //   42 transistors
  //   Mux4_1
  //   Seth Mueller
  //   max(s1+2.75, s0+4.75, d00+4, d01+4, d10+4, d11+4)
endmodule

module Mux2_1TransmissionGates (
  input  in0,
  input  in1,
  input  s,
  output z
);

  wire not_1_out, transmission_1_p4;

  not not_1 (not_1_out, s);
  // Transmission_Gate transmission_1: pin names not known; wires that end beside it: in0, s, not_1_out, transmission_1_p4
  not not_2 (z, transmission_1_p4);
  // Transmission_Gate transmission_2: pin names not known; wires that end beside it: in1, not_1_out, s, transmission_1_p4

  // Notes on the sheet:
  //   8 transistors
  //   Seth Mueller
  //   Mux2_1TransmissionGates
  //   max(s+1.75, in0+1, in1+1)
endmodule

module Mux4_1TransmissionGates (
  input  d00,
  input  d01,
  input  d10,
  input  d11,
  input  S0,
  input  S1,
  output O
);

  wire mux2_1transmissiongates_1_z, mux2_1transmissiongates_2_z;

  Mux2_1TransmissionGates mux2_1transmissiongates_1 (.in0(d00), .in1(d01), .s(S0), .z(mux2_1transmissiongates_1_z));
  Mux2_1TransmissionGates mux2_1transmissiongates_2 (.in0(d10), .in1(d11), .s(S0), .z(mux2_1transmissiongates_2_z));
  Mux2_1TransmissionGates mux2_1transmissiongates_3 (
    .in0(mux2_1transmissiongates_1_z), .in1(mux2_1transmissiongates_2_z), .s(S1), .z(O));

  // Notes on the sheet:
  //   24 transistors
  //   Seth Mueller
  //   Mux4_1TransmissionGates
  //   max(S1+1.75, S0+2.75, d00+2, d01+2, d10+2, d11+2)
endmodule

module Cin1Adder4Bit (
  input  [3:0] a,
  input  [3:0] b,
  output [3:0] s,
  output cout
);

  wire fa1_1_cout, faopt1_2_cout, faopt2_1_cout;

  FAopt1 faopt1_1 (.a(a[3]), .b(b[3]), .cin(faopt1_2_cout), .s(s[3]), .cout(cout));
  FAopt1 faopt1_2 (.a(a[2]), .b(b[2]), .cin(faopt2_1_cout), .s(s[2]), .cout(faopt1_2_cout));
  FAopt2 faopt2_1 (.a(a[1]), .b(b[1]), .cin(fa1_1_cout), .s(s[1]), .cout(faopt2_1_cout));
  FA1 fa1_1 (.b(b[0]), .a(a[0]), .s(s[0]), .cout(fa1_1_cout));

  // Notes on the sheet:
  //   8
  //   6
  //   8.75
  //   4
  //   6.75
  //   8.75
  //   8
  //   1.75
  //   5.5
  //   2.75
  //   Cin1Adder4Bit
  //   Seth Mueller
  //   120 transitors
endmodule

module Cin0Adder4Bit (
  input  [3:0] a,
  input  [3:0] b,
  output [3:0] s,
  output cout
);

  wire fa0_1_cout, faopt1_2_cout, faopt2_1_cout;

  FAopt1 faopt1_1 (.a(a[3]), .b(b[3]), .cin(faopt1_2_cout), .s(s[3]), .cout(cout));
  FAopt1 faopt1_2 (.a(a[2]), .b(b[2]), .cin(faopt2_1_cout), .s(s[2]), .cout(faopt1_2_cout));
  FAopt2 faopt2_1 (.a(a[1]), .b(b[1]), .cin(fa0_1_cout), .s(s[1]), .cout(faopt2_1_cout));
  FA0 fa0_1 (.b(b[0]), .a(a[0]), .s(s[0]), .cout(fa0_1_cout));

  // Notes on the sheet:
  //   8
  //   6
  //   8.75
  //   4
  //   6.75
  //   8.75
  //   8
  //   1.75
  //   5.5
  //   2.75
  //   Cin0Adder4Bit
  //   Seth Mueller
  //   120 transitors
endmodule

module CarrySelectAdder8Bit (
  input  [7:0] a,
  input  [7:0] b,
  output cout,
  output [7:0] s
);

  wire cin0adder4bit_1_cout, cin0adder4bit_2_cout, cin1adder4bit_1_cout, mux2_1transmissiongates_1_z,
       mux2_1transmissiongates_2_z, mux2_1transmissiongates_3_z, mux2_1transmissiongates_4_z,
       mux2_1transmissiongates_5_z;
  wire [3:0] cin0adder4bit_1_s, cin1adder4bit_1_s;

  Cin1Adder4Bit cin1adder4bit_1 (.a(a[7:4]), .b(b[7:4]), .s(cin1adder4bit_1_s), .cout(cin1adder4bit_1_cout));
  Cin0Adder4Bit cin0adder4bit_1 (.a(a[7:4]), .b(b[7:4]), .s(cin0adder4bit_1_s), .cout(cin0adder4bit_1_cout));
  Mux2_1TransmissionGates mux2_1transmissiongates_1 (
    .in0(cin0adder4bit_1_cout), .in1(cin1adder4bit_1_cout), .s(cin0adder4bit_2_cout),
    .z(mux2_1transmissiongates_1_z));
  Mux2_1TransmissionGates mux2_1transmissiongates_2 (
    .in0(cin0adder4bit_1_s[0]), .in1(cin1adder4bit_1_s[0]), .s(cin0adder4bit_2_cout),
    .z(mux2_1transmissiongates_2_z));
  Mux2_1TransmissionGates mux2_1transmissiongates_3 (
    .in0(cin0adder4bit_1_s[1]), .in1(cin1adder4bit_1_s[1]), .s(cin0adder4bit_2_cout),
    .z(mux2_1transmissiongates_3_z));
  Mux2_1TransmissionGates mux2_1transmissiongates_4 (
    .in0(cin0adder4bit_1_s[2]), .in1(cin1adder4bit_1_s[2]), .s(cin0adder4bit_2_cout),
    .z(mux2_1transmissiongates_4_z));
  Mux2_1TransmissionGates mux2_1transmissiongates_5 (
    .in0(cin0adder4bit_1_s[3]), .in1(cin1adder4bit_1_s[3]), .s(cin0adder4bit_2_cout),
    .z(mux2_1transmissiongates_5_z));
  not not_1 (cout, mux2_1transmissiongates_1_z);
  not not_2 (s[4], mux2_1transmissiongates_2_z);
  not not_3 (s[5], mux2_1transmissiongates_3_z);
  not not_4 (s[6], mux2_1transmissiongates_4_z);
  not not_5 (s[7], mux2_1transmissiongates_5_z);
  Cin0Adder4Bit cin0adder4bit_2 (.a(a[3:0]), .b(b[3:0]), .s(s[3:0]), .cout(cin0adder4bit_2_cout));

  // Notes on the sheet:
  //   8.75
  //   8
  //   8
  //   9.75
  //   8
  //   10.5
  //   Seth Mueller
  //   410 transitors
  //   10.5
  //   10.5
  //   CarrySelectAdder8Bit
endmodule

module CarrySelectAdder16Bit (
  input  [15:0] a,
  input  [15:0] b,
  output cout,
  output [15:0] s
);

  wire carryselectadder8bit_1_cout, carryselectadder8bit_2_cout, cin1carryselectadder8bit_1_cout,
       mux2_1transmissiongates_1_z, mux2_1transmissiongates_2_z, mux2_1transmissiongates_3_z,
       mux2_1transmissiongates_4_z, mux2_1transmissiongates_5_z, mux2_1transmissiongates_6_z,
       mux2_1transmissiongates_7_z, mux2_1transmissiongates_8_z, mux2_1transmissiongates_9_z;
  wire [7:0] carryselectadder8bit_1_s, cin1carryselectadder8bit_1_s;

  Cin1CarrySelectAdder8Bit cin1carryselectadder8bit_1 (
    .a(a[15:8]), .b(b[15:8]), .cout(cin1carryselectadder8bit_1_cout), .s(cin1carryselectadder8bit_1_s));
  CarrySelectAdder8Bit carryselectadder8bit_1 (
    .a(a[15:8]), .b(b[15:8]), .cout(carryselectadder8bit_1_cout), .s(carryselectadder8bit_1_s));
  Mux2_1TransmissionGates mux2_1transmissiongates_1 (
    .in0(carryselectadder8bit_1_cout), .in1(cin1carryselectadder8bit_1_cout),
    .s(carryselectadder8bit_2_cout), .z(mux2_1transmissiongates_1_z));
  Mux2_1TransmissionGates mux2_1transmissiongates_2 (
    .in0(carryselectadder8bit_1_s[0]), .in1(cin1carryselectadder8bit_1_s[0]),
    .s(carryselectadder8bit_2_cout), .z(mux2_1transmissiongates_2_z));
  Mux2_1TransmissionGates mux2_1transmissiongates_3 (
    .in0(carryselectadder8bit_1_s[1]), .in1(cin1carryselectadder8bit_1_s[1]),
    .s(carryselectadder8bit_2_cout), .z(mux2_1transmissiongates_3_z));
  Mux2_1TransmissionGates mux2_1transmissiongates_4 (
    .in0(carryselectadder8bit_1_s[2]), .in1(cin1carryselectadder8bit_1_s[2]),
    .s(carryselectadder8bit_2_cout), .z(mux2_1transmissiongates_4_z));
  Mux2_1TransmissionGates mux2_1transmissiongates_5 (
    .in0(carryselectadder8bit_1_s[3]), .in1(cin1carryselectadder8bit_1_s[3]),
    .s(carryselectadder8bit_2_cout), .z(mux2_1transmissiongates_5_z));
  Mux2_1TransmissionGates mux2_1transmissiongates_6 (
    .in0(carryselectadder8bit_1_s[4]), .in1(cin1carryselectadder8bit_1_s[4]),
    .s(carryselectadder8bit_2_cout), .z(mux2_1transmissiongates_6_z));
  Mux2_1TransmissionGates mux2_1transmissiongates_7 (
    .in0(carryselectadder8bit_1_s[5]), .in1(cin1carryselectadder8bit_1_s[5]),
    .s(carryselectadder8bit_2_cout), .z(mux2_1transmissiongates_7_z));
  Mux2_1TransmissionGates mux2_1transmissiongates_8 (
    .in0(carryselectadder8bit_1_s[6]), .in1(cin1carryselectadder8bit_1_s[6]),
    .s(carryselectadder8bit_2_cout), .z(mux2_1transmissiongates_8_z));
  Mux2_1TransmissionGates mux2_1transmissiongates_9 (
    .in0(carryselectadder8bit_1_s[7]), .in1(cin1carryselectadder8bit_1_s[7]),
    .s(carryselectadder8bit_2_cout), .z(mux2_1transmissiongates_9_z));
  not not_1 (cout, mux2_1transmissiongates_1_z);
  not not_2 (s[8], mux2_1transmissiongates_2_z);
  not not_3 (s[9], mux2_1transmissiongates_3_z);
  not not_4 (s[10], mux2_1transmissiongates_4_z);
  not not_5 (s[11], mux2_1transmissiongates_5_z);
  not not_6 (s[12], mux2_1transmissiongates_6_z);
  not not_7 (s[13], mux2_1transmissiongates_7_z);
  not not_8 (s[14], mux2_1transmissiongates_8_z);
  not not_9 (s[15], mux2_1transmissiongates_9_z);
  CarrySelectAdder8Bit carryselectadder8bit_2 (.a(a[7:0]), .b(b[7:0]), .cout(carryselectadder8bit_2_cout), .s(s[7:0]));

  // Notes on the sheet:
  //   10.5
  //   12.25
  //   10.5
  //   8
  //   Seth Mueller
  //   1320 transitors
  //   CarrySelectAdder8Bit
  //   13
  //   13
endmodule

module Cin1CarrySelectAdder8Bit (
  input  [7:0] a,
  input  [7:0] b,
  output cout,
  output [7:0] s
);

  wire cin0adder4bit_1_cout, cin1adder4bit_1_cout, cin1adder4bit_2_cout, mux2_1transmissiongates_1_z,
       mux2_1transmissiongates_2_z, mux2_1transmissiongates_3_z, mux2_1transmissiongates_4_z,
       mux2_1transmissiongates_5_z;
  wire [3:0] cin0adder4bit_1_s, cin1adder4bit_1_s;

  Cin1Adder4Bit cin1adder4bit_1 (.a(a[7:4]), .b(b[7:4]), .s(cin1adder4bit_1_s), .cout(cin1adder4bit_1_cout));
  Cin0Adder4Bit cin0adder4bit_1 (.a(a[7:4]), .b(b[7:4]), .s(cin0adder4bit_1_s), .cout(cin0adder4bit_1_cout));
  Mux2_1TransmissionGates mux2_1transmissiongates_1 (
    .in0(cin0adder4bit_1_cout), .in1(cin1adder4bit_1_cout), .s(cin1adder4bit_2_cout),
    .z(mux2_1transmissiongates_1_z));
  Mux2_1TransmissionGates mux2_1transmissiongates_2 (
    .in0(cin0adder4bit_1_s[0]), .in1(cin1adder4bit_1_s[0]), .s(cin1adder4bit_2_cout),
    .z(mux2_1transmissiongates_2_z));
  Mux2_1TransmissionGates mux2_1transmissiongates_3 (
    .in0(cin0adder4bit_1_s[1]), .in1(cin1adder4bit_1_s[1]), .s(cin1adder4bit_2_cout),
    .z(mux2_1transmissiongates_3_z));
  Mux2_1TransmissionGates mux2_1transmissiongates_4 (
    .in0(cin0adder4bit_1_s[2]), .in1(cin1adder4bit_1_s[2]), .s(cin1adder4bit_2_cout),
    .z(mux2_1transmissiongates_4_z));
  Mux2_1TransmissionGates mux2_1transmissiongates_5 (
    .in0(cin0adder4bit_1_s[3]), .in1(cin1adder4bit_1_s[3]), .s(cin1adder4bit_2_cout),
    .z(mux2_1transmissiongates_5_z));
  not not_1 (cout, mux2_1transmissiongates_1_z);
  not not_2 (s[4], mux2_1transmissiongates_2_z);
  not not_3 (s[5], mux2_1transmissiongates_3_z);
  not not_4 (s[6], mux2_1transmissiongates_4_z);
  not not_5 (s[7], mux2_1transmissiongates_5_z);
  Cin1Adder4Bit cin1adder4bit_2 (.a(a[3:0]), .b(b[3:0]), .s(s[3:0]), .cout(cin1adder4bit_2_cout));

  // Notes on the sheet:
  //   8.75
  //   8
  //   8
  //   9.75
  //   8
  //   10.5
  //   Seth Mueller
  //   410 transitors
  //   10.5
  //   10.5
  //   Cin1CarrySelectAdder8Bit
endmodule

module CarryLookAhead (
  input  P0,
  input  P1,
  input  Cin,
  input  P2,
  input  P3,
  input  G0,
  input  G1,
  input  G2,
  input  G3,
  output C4
);

  wire and_1_out, and_2_out, and_3_out, and_4_out, aoi21_1_y, nand_1_out, nand_2_out, nor_1_out;

  and and_1 (and_1_out, P2, P3);
  and and_2 (and_2_out, P2, P3, G1);
  and and_3 (and_3_out, P3, G2);
  and and_4 (and_4_out, P0, P1, and_1_out);
  nand nand_1 (nand_1_out, and_1_out, P1, G0);
  nor nor_1 (nor_1_out, and_2_out, and_3_out, G3);
  nand nand_2 (nand_2_out, nand_1_out, nor_1_out);
  AOI21 aoi21_1 (.A(nand_2_out), .B(and_4_out), .C(Cin), .Y(aoi21_1_y));
  not not_1 (C4, aoi21_1_y);

  // Notes on the sheet:
  //   7
  //   Seth Mueller
  //   CarryLookAhead
endmodule

module AOI21 (
  input  B,
  input  C,
  input  A,
  output Y
);

  wire transistor_1_out, transistor_6_out;

  Transistor transistor_1 (.in(1'b1), .out(transistor_1_out), .gate(B));
  Transistor #(.\type ("n")) transistor_2 (.in(1'b0), .out(Y), .gate(A));
  Transistor transistor_3 (.in(transistor_1_out), .out(Y), .gate(A));
  Transistor transistor_4 (.in(1'b1), .out(transistor_1_out), .gate(C));
  Transistor #(.\type ("n")) transistor_5 (.in(transistor_6_out), .out(Y), .gate(B));
  Transistor #(.\type ("n")) transistor_6 (.in(1'b0), .out(transistor_6_out), .gate(C));
endmodule

module AdderSubtractor16Bit (
  input  in_1,
  input  [15:0] B,
  input  [15:0] A,
  output [15:0] Y,
  output Overflow
);

  wire not_2_out, xor_1_out, xor_2_out;
  wire [15:0] multiplexer_1_out, not_1_out;

  Multiplexer #(.width(16)) multiplexer_1 (.in0(B), .in1(not_1_out), .out(multiplexer_1_out), .sel(in_1));
  assign not_1_out = ~B;  // NOT_Gate not_1, 16 bits wide
  Adder #(.width(16)) adder_1 (.a(multiplexer_1_out), .b(A), .out(Y), .cin(in_1));  // open: cout
  xor xor_1 (xor_1_out, Y[15], multiplexer_1_out[15]);
  xor xor_2 (xor_2_out, multiplexer_1_out[15], A[15]);
  not not_2 (not_2_out, xor_2_out);
  and and_1 (Overflow, xor_1_out, not_2_out);
endmodule

module CSAwithSubtraction16Bit (
  input  [15:0] A,
  input  [15:0] B,
  input  in_3,
  output [15:0] Y,
  output Overflow
);

  wire not_2_out, xor_1_out, xor_2_out;
  wire [15:0] multiplexer_1_out, not_1_out;

  assign not_1_out = ~B;  // NOT_Gate not_1, 16 bits wide
  Multiplexer #(.width(16)) multiplexer_1 (.in0(B), .in1(not_1_out), .out(multiplexer_1_out), .sel(in_3));
  CSAcin16Bit csacin16bit_1 (.a(A), .b(multiplexer_1_out), .cin(in_3), .s(Y));  // open: cout
  xor xor_1 (xor_1_out, Y[15], multiplexer_1_out[15]);
  xor xor_2 (xor_2_out, multiplexer_1_out[15], A[15]);
  not not_2 (not_2_out, xor_2_out);
  and and_1 (Overflow, xor_1_out, not_2_out);

  // Notes on the sheet:
  //   32767
endmodule

module CSAcin4Bit (
  input  [3:0] a,
  input  [3:0] b,
  input  Cin,
  output [3:0] s,
  output cout
);

  wire faopt1_2_cout, faopt1_3_cout, faopt2_1_cout;

  FAopt1 faopt1_1 (.a(a[3]), .b(b[3]), .cin(faopt1_2_cout), .s(s[3]), .cout(cout));
  FAopt1 faopt1_2 (.a(a[2]), .b(b[2]), .cin(faopt2_1_cout), .s(s[2]), .cout(faopt1_2_cout));
  FAopt2 faopt2_1 (.a(a[1]), .b(b[1]), .cin(faopt1_3_cout), .s(s[1]), .cout(faopt2_1_cout));
  FAopt1 faopt1_3 (.a(a[0]), .b(b[0]), .cin(Cin), .s(s[0]), .cout(faopt1_3_cout));

  // Notes on the sheet:
  //   8
  //   8.75
  //   8
  //   Cin0Adder4Bit
  //   Seth Mueller
  //   138 transitors
endmodule

module CSAcin8Bit (
  input  [7:0] a,
  input  [7:0] b,
  input  Cin,
  output cout,
  output [7:0] s
);

  wire cin0adder4bit_1_cout, cin1adder4bit_1_cout, csacin4bit_1_cout, mux2_1transmissiongates_1_z,
       mux2_1transmissiongates_2_z, mux2_1transmissiongates_3_z, mux2_1transmissiongates_4_z,
       mux2_1transmissiongates_5_z;
  wire [3:0] cin0adder4bit_1_s, cin1adder4bit_1_s;

  Cin1Adder4Bit cin1adder4bit_1 (.a(a[7:4]), .b(b[7:4]), .s(cin1adder4bit_1_s), .cout(cin1adder4bit_1_cout));
  Cin0Adder4Bit cin0adder4bit_1 (.a(a[7:4]), .b(b[7:4]), .s(cin0adder4bit_1_s), .cout(cin0adder4bit_1_cout));
  Mux2_1TransmissionGates mux2_1transmissiongates_1 (
    .in0(cin0adder4bit_1_cout), .in1(cin1adder4bit_1_cout), .s(csacin4bit_1_cout),
    .z(mux2_1transmissiongates_1_z));
  Mux2_1TransmissionGates mux2_1transmissiongates_2 (
    .in0(cin0adder4bit_1_s[0]), .in1(cin1adder4bit_1_s[0]), .s(csacin4bit_1_cout),
    .z(mux2_1transmissiongates_2_z));
  Mux2_1TransmissionGates mux2_1transmissiongates_3 (
    .in0(cin0adder4bit_1_s[1]), .in1(cin1adder4bit_1_s[1]), .s(csacin4bit_1_cout),
    .z(mux2_1transmissiongates_3_z));
  Mux2_1TransmissionGates mux2_1transmissiongates_4 (
    .in0(cin0adder4bit_1_s[2]), .in1(cin1adder4bit_1_s[2]), .s(csacin4bit_1_cout),
    .z(mux2_1transmissiongates_4_z));
  Mux2_1TransmissionGates mux2_1transmissiongates_5 (
    .in0(cin0adder4bit_1_s[3]), .in1(cin1adder4bit_1_s[3]), .s(csacin4bit_1_cout),
    .z(mux2_1transmissiongates_5_z));
  not not_1 (cout, mux2_1transmissiongates_1_z);
  not not_2 (s[4], mux2_1transmissiongates_2_z);
  not not_3 (s[5], mux2_1transmissiongates_3_z);
  not not_4 (s[6], mux2_1transmissiongates_4_z);
  not not_5 (s[7], mux2_1transmissiongates_5_z);
  CSAcin4Bit csacin4bit_1 (.a(a[3:0]), .b(b[3:0]), .Cin(Cin), .s(s[3:0]), .cout(csacin4bit_1_cout));

  // Notes on the sheet:
  //   8.75
  //   8
  //   8
  //   9.75
  //   8
  //   10.5
  //   Seth Mueller
  //   428 transitors
  //   10.5
  //   10.5
  //   CarrySelectAdder8Bit
endmodule

module CSAcin16Bit (
  input  [15:0] a,
  input  [15:0] b,
  input  cin,
  output cout,
  output [15:0] s
);

  wire carryselectadder8bit_1_cout, cin1carryselectadder8bit_1_cout, csacin8bit_1_cout,
       mux2_1transmissiongates_1_z, mux2_1transmissiongates_2_z, mux2_1transmissiongates_3_z,
       mux2_1transmissiongates_4_z, mux2_1transmissiongates_5_z, mux2_1transmissiongates_6_z,
       mux2_1transmissiongates_7_z, mux2_1transmissiongates_8_z, mux2_1transmissiongates_9_z;
  wire [7:0] carryselectadder8bit_1_s, cin1carryselectadder8bit_1_s;

  Cin1CarrySelectAdder8Bit cin1carryselectadder8bit_1 (
    .a(a[15:8]), .b(b[15:8]), .cout(cin1carryselectadder8bit_1_cout), .s(cin1carryselectadder8bit_1_s));
  CarrySelectAdder8Bit carryselectadder8bit_1 (
    .a(a[15:8]), .b(b[15:8]), .cout(carryselectadder8bit_1_cout), .s(carryselectadder8bit_1_s));
  Mux2_1TransmissionGates mux2_1transmissiongates_1 (
    .in0(carryselectadder8bit_1_cout), .in1(cin1carryselectadder8bit_1_cout), .s(csacin8bit_1_cout),
    .z(mux2_1transmissiongates_1_z));
  Mux2_1TransmissionGates mux2_1transmissiongates_2 (
    .in0(carryselectadder8bit_1_s[0]), .in1(cin1carryselectadder8bit_1_s[0]), .s(csacin8bit_1_cout),
    .z(mux2_1transmissiongates_2_z));
  Mux2_1TransmissionGates mux2_1transmissiongates_3 (
    .in0(carryselectadder8bit_1_s[1]), .in1(cin1carryselectadder8bit_1_s[1]), .s(csacin8bit_1_cout),
    .z(mux2_1transmissiongates_3_z));
  Mux2_1TransmissionGates mux2_1transmissiongates_4 (
    .in0(carryselectadder8bit_1_s[2]), .in1(cin1carryselectadder8bit_1_s[2]), .s(csacin8bit_1_cout),
    .z(mux2_1transmissiongates_4_z));
  Mux2_1TransmissionGates mux2_1transmissiongates_5 (
    .in0(carryselectadder8bit_1_s[3]), .in1(cin1carryselectadder8bit_1_s[3]), .s(csacin8bit_1_cout),
    .z(mux2_1transmissiongates_5_z));
  Mux2_1TransmissionGates mux2_1transmissiongates_6 (
    .in0(carryselectadder8bit_1_s[4]), .in1(cin1carryselectadder8bit_1_s[4]), .s(csacin8bit_1_cout),
    .z(mux2_1transmissiongates_6_z));
  Mux2_1TransmissionGates mux2_1transmissiongates_7 (
    .in0(carryselectadder8bit_1_s[5]), .in1(cin1carryselectadder8bit_1_s[5]), .s(csacin8bit_1_cout),
    .z(mux2_1transmissiongates_7_z));
  Mux2_1TransmissionGates mux2_1transmissiongates_8 (
    .in0(carryselectadder8bit_1_s[6]), .in1(cin1carryselectadder8bit_1_s[6]), .s(csacin8bit_1_cout),
    .z(mux2_1transmissiongates_8_z));
  Mux2_1TransmissionGates mux2_1transmissiongates_9 (
    .in0(carryselectadder8bit_1_s[7]), .in1(cin1carryselectadder8bit_1_s[7]), .s(csacin8bit_1_cout),
    .z(mux2_1transmissiongates_9_z));
  not not_1 (cout, mux2_1transmissiongates_1_z);
  not not_2 (s[8], mux2_1transmissiongates_2_z);
  not not_3 (s[9], mux2_1transmissiongates_3_z);
  not not_4 (s[10], mux2_1transmissiongates_4_z);
  not not_5 (s[11], mux2_1transmissiongates_5_z);
  not not_6 (s[12], mux2_1transmissiongates_6_z);
  not not_7 (s[13], mux2_1transmissiongates_7_z);
  not not_8 (s[14], mux2_1transmissiongates_8_z);
  not not_9 (s[15], mux2_1transmissiongates_9_z);
  CSAcin8Bit csacin8bit_1 (.a(a[7:0]), .b(b[7:0]), .Cin(cin), .cout(csacin8bit_1_cout), .s(s[7:0]));

  // Notes on the sheet:
  //   10.5
  //   12.25
  //   10.5
  //   8
  //   Seth Mueller
  //   1320 transitors
  //   CarrySelectAdder8Bit
  //   13
  //   13
endmodule

module overflowchecker (
  input  B3,
  input  OP,
  input  R3,
  input  A3,
  output overflow
);

  wire multiplexer_1_out, not_1_out, not_2_out, xor_1_out, xor_2_out;

  not not_1 (not_1_out, B3);
  Multiplexer multiplexer_1 (.in0(B3), .in1(not_1_out), .out(multiplexer_1_out), .sel(OP));
  xor xor_1 (xor_1_out, multiplexer_1_out, R3);
  xor xor_2 (xor_2_out, multiplexer_1_out, A3);
  not not_2 (not_2_out, xor_2_out);
  and and_1 (overflow, xor_1_out, not_2_out);
endmodule

module R0R1 (
  input  rst,
  input  subtract,
  input  [15:0] R1in
);

  wire clk;
  wire [15:0] csawithsubtraction16bit_1_y, R0, register_2_q;

  Clock u_clk (.out(clk));
  Register #(.width(16)) register_1 (.D(csawithsubtraction16bit_1_y), .en(1'b1), .clk(clk), .Q(R0), .clr(rst));
  Register #(.width(16)) register_2 (.D(R1in), .en(1'b1), .clk(clk), .Q(register_2_q), .clr(rst));
  CSAwithSubtraction16Bit csawithsubtraction16bit_1 (
    .A(R0), .B(register_2_q), .in_3(subtract), .Y(csawithsubtraction16bit_1_y));  // open: Overflow
  Hex_Digit_Display hex_digit_display_1 (.value(R0[15:12]));  // open: dp
  Hex_Digit_Display hex_digit_display_2 (.value(R0[11:8]));  // open: dp
  Hex_Digit_Display hex_digit_display_3 (.value(R0[7:4]));  // open: dp
  Hex_Digit_Display hex_digit_display_4 (.value(R0[3:0]));  // open: dp

  // Notes on the sheet:
  //   9 clock cycles
  //   4 to bring it to zero
  //   5 to get to 107 (first is loading 27 into R1)
endmodule

module TestRegisters (
  input  rst,
  input  subtract,
  input  [1:0] Rd,
  input  [1:0] Rs
);

  wire clk, csawithsubtraction16bit_1_overflow, register_1_q, regwe_1_reg0we, regwe_1_reg1we, regwe_1_reg2we,
       regwe_1_reg3we;
  wire [15:0] csawithsubtraction16bit_1_y, R0, R1, R2, R3, srcsel_1_regout, srcsel_2_regout;

  Hex_Digit_Display hex_digit_display_1 (.value(R0[15:12]));  // open: dp
  Hex_Digit_Display hex_digit_display_2 (.value(R0[11:8]));  // open: dp
  Hex_Digit_Display hex_digit_display_3 (.value(R2[15:12]));  // open: dp
  Hex_Digit_Display hex_digit_display_4 (.value(R2[11:8]));  // open: dp
  Hex_Digit_Display hex_digit_display_5 (.value(R0[7:4]));  // open: dp
  Hex_Digit_Display hex_digit_display_6 (.value(R0[3:0]));  // open: dp
  Hex_Digit_Display hex_digit_display_7 (.value(R2[7:4]));  // open: dp
  Hex_Digit_Display hex_digit_display_8 (.value(R2[3:0]));  // open: dp
  Clock u_clk (.out(clk));
  Hex_Digit_Display hex_digit_display_9 (.value(R1[15:12]));  // open: dp
  Hex_Digit_Display hex_digit_display_10 (.value(R3[15:12]));  // open: dp
  srcSel srcsel_1 (.reg0(R0), .reg1(R1), .reg2(R2), .reg3(R3), .sel(Rd), .regOut(srcsel_1_regout));
  srcSel srcsel_2 (.reg0(R0), .reg1(R1), .reg2(R2), .reg3(R3), .sel(Rs), .regOut(srcsel_2_regout));
  Hex_Digit_Display hex_digit_display_11 (.value(R1[11:8]));  // open: dp
  Hex_Digit_Display hex_digit_display_12 (.value(R1[7:4]));  // open: dp
  Hex_Digit_Display hex_digit_display_13 (.value(R3[11:8]));  // open: dp
  Hex_Digit_Display hex_digit_display_14 (.value(R3[7:4]));  // open: dp
  Hex_Digit_Display hex_digit_display_15 (.value(R1[3:0]));  // open: dp
  Hex_Digit_Display hex_digit_display_16 (.value(R3[3:0]));  // open: dp
  CSAwithSubtraction16Bit csawithsubtraction16bit_1 (
    .A(srcsel_1_regout), .B(srcsel_2_regout), .in_3(subtract), .Y(csawithsubtraction16bit_1_y),
    .Overflow(csawithsubtraction16bit_1_overflow));
  regWE regwe_1 (
    .Rd(Rd), .regWrite(1'b1), .reg0WE(regwe_1_reg0we), .reg1WE(regwe_1_reg1we), .reg2WE(regwe_1_reg2we),
    .reg3WE(regwe_1_reg3we));
  Register #(.width(1)) register_1 (
    .D(1'b1), .en(csawithsubtraction16bit_1_overflow), .clk(clk), .Q(register_1_q), .clr(rst));
  LED led_1 (.in(register_1_q));
  Register #(.width(16)) u_R0 (.D(csawithsubtraction16bit_1_y), .en(regwe_1_reg0we), .clk(clk), .Q(R0), .clr(rst));
  Register #(.width(16)) u_R1 (.D(csawithsubtraction16bit_1_y), .en(regwe_1_reg1we), .clk(clk), .Q(R1), .clr(rst));
  Register #(.width(16)) u_R2 (.D(csawithsubtraction16bit_1_y), .en(regwe_1_reg2we), .clk(clk), .Q(R2), .clr(rst));
  Register #(.width(16)) u_R3 (.D(csawithsubtraction16bit_1_y), .en(regwe_1_reg3we), .clk(clk), .Q(R3), .clr(rst));

  // Notes on the sheet:
  //   R0
  //   R2
  //   R1
  //   R3
  //   4c41
  //   5341
  //   7b43
  //   537d
endmodule

module regWE (
  input  [1:0] Rd,
  input  regWrite,
  output reg0WE,
  output reg1WE,
  output reg2WE,
  output reg3WE
);

  wire not_1_out, not_2_out, not_3_out, not_4_out;

  not not_1 (not_1_out, Rd[1]);
  not not_2 (not_2_out, Rd[0]);
  not not_3 (not_3_out, Rd[1]);
  not not_4 (not_4_out, Rd[0]);
  and and_1 (reg0WE, not_1_out, not_2_out, regWrite);
  and and_2 (reg1WE, not_3_out, Rd[0], regWrite);
  and and_3 (reg2WE, Rd[1], not_4_out, regWrite);
  and and_4 (reg3WE, Rd[1], Rd[0], regWrite);
endmodule

module srcSel (
  input  [15:0] reg0,
  input  [15:0] reg1,
  input  [15:0] reg2,
  input  [15:0] reg3,
  input  [1:0] sel,
  output [15:0] regOut
);

  wire [15:0] multiplexer_1_out, multiplexer_2_out;

  Multiplexer #(.width(16)) multiplexer_1 (.in0(reg0), .in1(reg1), .out(multiplexer_1_out), .sel(sel[0]));
  Multiplexer #(.width(16)) multiplexer_2 (.in0(reg2), .in1(reg3), .out(multiplexer_2_out), .sel(sel[0]));
  Multiplexer #(.width(16)) multiplexer_3 (
    .in0(multiplexer_1_out), .in1(multiplexer_2_out), .out(regOut), .sel(sel[1]));
endmodule

module ProgramCounter (
  input  clk,
  input  rst,
  output [5:0] pc
);

  wire [5:0] adder_1_out;

  Adder #(.width(6)) adder_1 (.a(6'b000001), .b(pc), .out(adder_1_out));  // open: cin, cout
  Register #(.width(6)) register_1 (.D(adder_1_out), .en(1'b1), .clk(clk), .Q(pc), .clr(rst));
endmodule

module FirstProgram (
  input  rst
);

  wire and_1_out, clk, csawithsubtraction16bit_1_overflow, not_1_out, not_2_out, not_3_out, not_4_out,
       register_1_q, regwe_1_reg0we, regwe_1_reg1we, regwe_1_reg2we, regwe_1_reg3we, RegWrite, Subtract;
  wire [0:0] t_ff_1_q;
  wire [1:0] Rd, Rs;
  wire [3:0] ram_1_dout;
  wire [15:0] csawithsubtraction16bit_1_y, R0, R1, R2, R3, srcsel_1_regout, srcsel_2_regout;

  T_Flip_Flop t_ff_1 (.T(1'b1), .clk(clk), .Q(t_ff_1_q[0]));  // open: Qn, reset, preset
  ProgramCounter programcounter_1 (.clk(clk), .rst(rst));  // open: pc
  not not_1 (not_1_out, ram_1_dout[3]);
  not not_2 (not_2_out, ram_1_dout[2]);
  not not_3 (not_3_out, ram_1_dout[1]);
  not not_4 (not_4_out, ram_1_dout[0]);
  RAM #(.addrWidth(6), .asyncread("true"), .trigger("falling")) ram_1 (
    .addr({{5{1'b0}}, t_ff_1_q[0]}), .we(1'b0), .oe(1'b1), .clk(clk), .dout({Rd, Rs, ram_1_dout}));  // open: din
  and and_1 (and_1_out, not_4_out, ram_1_dout[1], not_2_out, not_1_out);
  and and_2 (Subtract, ram_1_dout[0], ram_1_dout[1], not_2_out, not_1_out);
  or or_1 (RegWrite, and_1_out, Subtract);
  Clock u_clk (.out(clk));
  Hex_Digit_Display hex_digit_display_1 (.value(R0[15:12]));  // open: dp
  Hex_Digit_Display hex_digit_display_2 (.value(R2[15:12]));  // open: dp
  Hex_Digit_Display hex_digit_display_3 (.value(R0[11:8]));  // open: dp
  Hex_Digit_Display hex_digit_display_4 (.value(R0[7:4]));  // open: dp
  // Probe on R0
  Hex_Digit_Display hex_digit_display_5 (.value(R2[11:8]));  // open: dp
  Hex_Digit_Display hex_digit_display_6 (.value(R2[7:4]));  // open: dp
  // Probe on R2
  Hex_Digit_Display hex_digit_display_7 (.value(R0[3:0]));  // open: dp
  Hex_Digit_Display hex_digit_display_8 (.value(R2[3:0]));  // open: dp
  Hex_Digit_Display hex_digit_display_9 (.value(R1[15:12]));  // open: dp
  Hex_Digit_Display hex_digit_display_10 (.value(R1[11:8]));  // open: dp
  Hex_Digit_Display hex_digit_display_11 (.value(R3[15:12]));  // open: dp
  Hex_Digit_Display hex_digit_display_12 (.value(R3[11:8]));  // open: dp
  srcSel srcsel_1 (.reg0(R0), .reg1(R1), .reg2(R2), .reg3(R3), .sel(Rd), .regOut(srcsel_1_regout));
  srcSel srcsel_2 (.reg0(R0), .reg1(R1), .reg2(R2), .reg3(R3), .sel(Rs), .regOut(srcsel_2_regout));
  Hex_Digit_Display hex_digit_display_13 (.value(R1[7:4]));  // open: dp
  Hex_Digit_Display hex_digit_display_14 (.value(R1[3:0]));  // open: dp
  // Probe on R1
  Hex_Digit_Display hex_digit_display_15 (.value(R3[7:4]));  // open: dp
  Hex_Digit_Display hex_digit_display_16 (.value(R3[3:0]));  // open: dp
  LED led_1 (.in(register_1_q));
  CSAwithSubtraction16Bit csawithsubtraction16bit_1 (
    .A(srcsel_1_regout), .B(srcsel_2_regout), .in_3(Subtract), .Y(csawithsubtraction16bit_1_y),
    .Overflow(csawithsubtraction16bit_1_overflow));
  regWE regwe_1 (
    .Rd(Rd), .regWrite(RegWrite), .reg0WE(regwe_1_reg0we), .reg1WE(regwe_1_reg1we), .reg2WE(regwe_1_reg2we),
    .reg3WE(regwe_1_reg3we));
  Register #(.width(1)) register_1 (
    .D(1'b1), .en(csawithsubtraction16bit_1_overflow), .clk(clk), .Q(register_1_q), .clr(rst));
  Register #(.width(16)) u_R0 (.D(csawithsubtraction16bit_1_y), .en(regwe_1_reg0we), .clk(clk), .Q(R0), .clr(rst));
  Register #(.width(16)) u_R1 (.D(csawithsubtraction16bit_1_y), .en(regwe_1_reg1we), .clk(clk), .Q(R1), .clr(rst));
  Register #(.width(16)) u_R2 (.D(csawithsubtraction16bit_1_y), .en(regwe_1_reg2we), .clk(clk), .Q(R2), .clr(rst));
  Register #(.width(16)) u_R3 (.D(csawithsubtraction16bit_1_y), .en(regwe_1_reg3we), .clk(clk), .Q(R3), .clr(rst));

  // Notes on the sheet:
  //   +
  //   -
  //   R0
  //   R2
  //   R1
  //   R3
  //   4c41
  //   5341
  //   7b43
  //   537d
endmodule

module FirstProgramLASTTIME (
  input  rst
);

  wire and_1_out, clk, csawithsubtraction16bit_1_overflow, overflow, regwe_1_reg0we, regwe_1_reg1we,
       regwe_1_reg2we, regwe_1_reg3we, RegWrite, Subtract;
  wire [1:0] Rd, Rs;
  wire [5:0] programcounter_1_pc;
  wire [7:0] ram_1_dout, register_1_q;
  wire [15:0] csawithsubtraction16bit_1_y, R0, R1, R2, R3, srcsel_1_regout, srcsel_2_regout;

  Hex_Digit_Display hex_digit_display_1 (.value(R0[15:12]));  // open: dp
  Hex_Digit_Display hex_digit_display_2 (.value(R2[15:12]));  // open: dp
  Clock u_clk (.out(clk));
  ProgramCounter programcounter_1 (.clk(clk), .rst(rst), .pc(programcounter_1_pc));
  Hex_Digit_Display hex_digit_display_3 (.value(R0[11:8]));  // open: dp
  Hex_Digit_Display hex_digit_display_4 (.value(R0[7:4]));  // open: dp
  // Probe on R0
  Hex_Digit_Display hex_digit_display_5 (.value(R2[11:8]));  // open: dp
  Hex_Digit_Display hex_digit_display_6 (.value(R2[7:4]));  // open: dp
  // Probe on R2
  Hex_Digit_Display hex_digit_display_7 (.value(R0[3:0]));  // open: dp
  Hex_Digit_Display hex_digit_display_8 (.value(R2[3:0]));  // open: dp
  Hex_Digit_Display hex_digit_display_9 (.value(R1[15:12]));  // open: dp
  Hex_Digit_Display hex_digit_display_10 (.value(R1[11:8]));  // open: dp
  Hex_Digit_Display hex_digit_display_11 (.value(R3[15:12]));  // open: dp
  Hex_Digit_Display hex_digit_display_12 (.value(R3[11:8]));  // open: dp
  LED led_1 (.in(overflow));
  RAM #(.addrWidth(6), .asyncread("true"), .trigger("falling")) ram_1 (
    .addr(programcounter_1_pc), .we(1'b0), .oe(1'b1), .clk(clk), .dout(ram_1_dout));  // open: din
  Hex_Digit_Display hex_digit_display_13 (.value(R1[7:4]));  // open: dp
  Hex_Digit_Display hex_digit_display_14 (.value(R1[3:0]));  // open: dp
  // Probe on R1
  Hex_Digit_Display hex_digit_display_15 (.value(R3[7:4]));  // open: dp
  Hex_Digit_Display hex_digit_display_16 (.value(R3[3:0]));  // open: dp
  Register register_1 (.D(ram_1_dout), .en(1'b1), .clk(clk), .Q(register_1_q), .clr(rst));
  srcSel srcsel_1 (.reg0(R0), .reg1(R1), .reg2(R2), .reg3(R3), .sel(Rd), .regOut(srcsel_1_regout));
  srcSel srcsel_2 (.reg0(R0), .reg1(R1), .reg2(R2), .reg3(R3), .sel(Rs), .regOut(srcsel_2_regout));
  regWE regwe_1 (
    .Rd(Rd), .regWrite(RegWrite), .reg0WE(regwe_1_reg0we), .reg1WE(regwe_1_reg1we), .reg2WE(regwe_1_reg2we),
    .reg3WE(regwe_1_reg3we));
  // IRDecoder irdecoder_1: pin names not known; wires that end beside it: Rd, Rs, RegWrite, Subtract
  CSAwithSubtraction16Bit csawithsubtraction16bit_1 (
    .A(srcsel_1_regout), .B(srcsel_2_regout), .in_3(Subtract), .Y(csawithsubtraction16bit_1_y),
    .Overflow(csawithsubtraction16bit_1_overflow));
  and and_1 (and_1_out, RegWrite, csawithsubtraction16bit_1_overflow);
  Register #(.width(16)) u_R0 (.D(csawithsubtraction16bit_1_y), .en(regwe_1_reg0we), .clk(clk), .Q(R0), .clr(rst));
  Register #(.width(16)) u_R1 (.D(csawithsubtraction16bit_1_y), .en(regwe_1_reg1we), .clk(clk), .Q(R1), .clr(rst));
  Register #(.width(16)) u_R2 (.D(csawithsubtraction16bit_1_y), .en(regwe_1_reg2we), .clk(clk), .Q(R2), .clr(rst));
  Register #(.width(16)) u_R3 (.D(csawithsubtraction16bit_1_y), .en(regwe_1_reg3we), .clk(clk), .Q(R3), .clr(rst));
  Register #(.width(1)) register_2 (.D(1'b1), .en(and_1_out), .clk(clk), .Q(overflow), .clr(rst));

  // Notes on the sheet:
  //   R0
  //   R2
  //   R1
  //   R3
  //   INSTRUCTION STAGE
  //   DECODE STAGE
  //   4c41
  //   5341
  //   7b43
  //   537d
endmodule

module IRDecoder (
  input  [7:0] IR,
  input  rst,
  input  clk,
  output [1:0] Rd,
  output [1:0] Rs,
  output writeenable,
  output add,
  output sub,
  output ldi,
  output ld
);

  wire and_1_out, and_2_out, and_3_out, and_4_out, not_1_out, not_2_out, not_3_out, not_4_out, or_1_out;

  not not_1 (not_1_out, IR[3]);
  not not_2 (not_2_out, IR[2]);
  not not_3 (not_3_out, IR[1]);
  not not_4 (not_4_out, IR[0]);
  Register #(.width(2)) register_1 (.D(IR[7:6]), .en(1'b1), .clk(clk), .Q(Rd), .clr(rst));
  Register #(.width(2)) register_2 (.D(IR[5:4]), .en(1'b1), .clk(clk), .Q(Rs), .clr(rst));
  and and_1 (and_1_out, not_4_out, IR[1], not_2_out, not_1_out);
  and and_2 (and_2_out, IR[0], IR[1], not_2_out, not_1_out);
  and and_3 (and_3_out, IR[3], IR[2], IR[1], not_4_out);
  and and_4 (and_4_out, IR[3], IR[2], IR[1], IR[0]);
  or or_1 (or_1_out, and_1_out, and_3_out, and_4_out, and_2_out);
  Register #(.width(1)) register_3 (.D(or_1_out), .en(1'b1), .clk(clk), .Q(writeenable), .clr(rst));
  Register #(.width(1)) register_4 (.D(and_1_out), .en(1'b1), .clk(clk), .Q(add), .clr(rst));
  Register #(.width(1)) register_5 (.D(and_2_out), .en(1'b1), .clk(clk), .Q(sub), .clr(rst));
  Register #(.width(1)) register_6 (.D(and_3_out), .en(1'b1), .clk(clk), .Q(ldi), .clr(rst));
  Register #(.width(1)) register_7 (.D(and_4_out), .en(1'b1), .clk(clk), .Q(ld), .clr(rst));
  Register #(.width(1)) register_8 (.en(1'b1), .clk(clk), .clr(rst));  // open: D, Q

  // Notes on the sheet:
  //   +
  //   -
  //   ldi
  //   ld
endmodule

module LoadingData (
  input  rst
);

  wire add, and_1_out, clk, csawithsubtraction16bit_1_overflow, ld, ldi, overflow, regwe_1_reg0we,
       regwe_1_reg1we, regwe_1_reg2we, regwe_1_reg3we, RegWriteBool, sub;
  wire [1:0] Rd, Rs;
  wire [5:0] programcounter_1_pc;
  wire [7:0] ram_1_dout, register_1_q;
  wire [15:0] AdderOut, R0, R1, R2, R3, RAMOut, RdVal, RegWriteVal, RsVal;

  Hex_Digit_Display hex_digit_display_1 (.value(R0[15:12]));  // open: dp
  Hex_Digit_Display hex_digit_display_2 (.value(R2[15:12]));  // open: dp
  Clock u_clk (.out(clk));
  ProgramCounter programcounter_1 (.clk(clk), .rst(rst), .pc(programcounter_1_pc));
  Hex_Digit_Display hex_digit_display_3 (.value(R0[11:8]));  // open: dp
  Hex_Digit_Display hex_digit_display_4 (.value(R0[7:4]));  // open: dp
  // Probe on R0
  Hex_Digit_Display hex_digit_display_5 (.value(R2[11:8]));  // open: dp
  Hex_Digit_Display hex_digit_display_6 (.value(R2[7:4]));  // open: dp
  // Probe on R2
  Hex_Digit_Display hex_digit_display_7 (.value(R0[3:0]));  // open: dp
  Hex_Digit_Display hex_digit_display_8 (.value(R2[3:0]));  // open: dp
  Hex_Digit_Display hex_digit_display_9 (.value(R1[15:12]));  // open: dp
  Hex_Digit_Display hex_digit_display_10 (.value(R1[11:8]));  // open: dp
  Hex_Digit_Display hex_digit_display_11 (.value(R3[15:12]));  // open: dp
  Hex_Digit_Display hex_digit_display_12 (.value(R3[11:8]));  // open: dp
  LED led_1 (.in(overflow));
  RAM #(.addrWidth(6), .asyncread("true"), .trigger("falling")) ram_1 (
    .addr(programcounter_1_pc), .we(1'b0), .oe(1'b1), .clk(clk), .dout(ram_1_dout));  // open: din
  Hex_Digit_Display hex_digit_display_13 (.value(R1[7:4]));  // open: dp
  Hex_Digit_Display hex_digit_display_14 (.value(R1[3:0]));  // open: dp
  // Probe on R1
  Hex_Digit_Display hex_digit_display_15 (.value(R3[7:4]));  // open: dp
  Hex_Digit_Display hex_digit_display_16 (.value(R3[3:0]));  // open: dp
  Register register_1 (.D(ram_1_dout), .en(1'b1), .clk(clk), .Q(register_1_q), .clr(rst));
  IRDecoder irdecoder_1 (
    .rst(rst), .clk(clk), .IR(register_1_q), .add(add), .sub(sub), .ldi(ldi), .ld(ld),
    .writeenable(RegWriteBool), .Rd(Rd), .Rs(Rs));
  RAM #(.addrWidth(16), .asyncread("true"), .dataWidth(16), .trigger("falling")) ram_2 (
    .addr(RsVal), .we(1'b0), .oe(1'b1), .clk(clk), .dout(RAMOut));  // open: din
  srcSel srcsel_1 (.reg0(R0), .reg1(R1), .reg2(R2), .reg3(R3), .sel(Rd), .regOut(RdVal));
  srcSel srcsel_2 (.reg0(R0), .reg1(R1), .reg2(R2), .reg3(R3), .sel(Rs), .regOut(RsVal));
  CSAwithSubtraction16Bit csawithsubtraction16bit_1 (
    .A(RdVal), .B(RsVal), .in_3(sub), .Y(AdderOut), .Overflow(csawithsubtraction16bit_1_overflow));
  DataSelect dataselect_1 (
    .Rs(Rs), .RAMresult(RAMOut), .ALUresult(AdderOut), .add(add), .sub(sub), .ld(ld), .ldi(ldi),
    .RdVal(RdVal), .RsVal(RsVal), .Rd(Rd), .data(RegWriteVal));
  regWE regwe_1 (
    .Rd(Rd), .regWrite(RegWriteBool), .reg0WE(regwe_1_reg0we), .reg1WE(regwe_1_reg1we),
    .reg2WE(regwe_1_reg2we), .reg3WE(regwe_1_reg3we));
  and and_1 (and_1_out, RegWriteBool, csawithsubtraction16bit_1_overflow);
  Register #(.width(1)) register_2 (.D(1'b1), .en(and_1_out), .clk(clk), .Q(overflow), .clr(rst));
  Register #(.width(16)) u_R0 (.D(RegWriteVal), .en(regwe_1_reg0we), .clk(clk), .Q(R0), .clr(rst));
  Register #(.width(16)) u_R1 (.D(RegWriteVal), .en(regwe_1_reg1we), .clk(clk), .Q(R1), .clr(rst));
  Register #(.width(16)) u_R2 (.D(RegWriteVal), .en(regwe_1_reg2we), .clk(clk), .Q(R2), .clr(rst));
  Register #(.width(16)) u_R3 (.D(RegWriteVal), .en(regwe_1_reg3we), .clk(clk), .Q(R3), .clr(rst));

  // Notes on the sheet:
  //   R0
  //   R2
  //   R1
  //   R3
  //   INSTRUCTION STAGE
  //   DECODE STAGE
  //   4c41
  //   5341
  //   7b43
  //   537d
endmodule

module DataSelect (
  input  [1:0] Rs,
  input  [15:0] RAMresult,
  input  [15:0] ALUresult,
  input  add,
  input  sub,
  input  ld,
  input  ldi,
  input  [15:0] RdVal,
  input  [15:0] RsVal,
  input  [1:0] Rd,
  output [15:0] data
);

  wire or_1_out;
  wire [15:0] multiplexer_1_out, multiplexer_2_out;

  or or_1 (or_1_out, add, sub);
  Multiplexer #(.width(16)) multiplexer_1 (.in0({16{1'b0}}), .in1(ALUresult), .out(multiplexer_1_out), .sel(or_1_out));
  Multiplexer #(.width(16)) multiplexer_2 (.in0(multiplexer_1_out), .in1(RAMresult), .out(multiplexer_2_out), .sel(ld));
  Multiplexer #(.width(16)) multiplexer_3 (.in0(multiplexer_2_out), .in1({{14{1'b0}}, Rs}), .out(data), .sel(ldi));
endmodule

module AddSub32Bit (
  input  Input_1,
  input  [31:0] B,
  input  [31:0] A,
  output [31:0] Y,
  output Overflow
);

  wire not_2_out, xor_1_out, xor_2_out;
  wire [31:0] multiplexer_1_out, not_1_out;

  Multiplexer #(.width(32)) multiplexer_1 (.in0(B), .in1(not_1_out), .out(multiplexer_1_out), .sel(Input_1));
  assign not_1_out = ~B;  // NOT_Gate not_1, 32 bits wide
  Adder #(.width(32)) adder_1 (.a(multiplexer_1_out), .b(A), .out(Y), .cin(Input_1));  // open: cout
  xor xor_1 (xor_1_out, Y[31], multiplexer_1_out[31]);
  xor xor_2 (xor_2_out, multiplexer_1_out[31], A[31]);
  not not_2 (not_2_out, xor_2_out);
  and and_1 (Overflow, xor_1_out, not_2_out);
endmodule

module rrisc (
  input  Input_1,
  input  Input_2
);

  wire branchCondition_1_jump, \break , clk, EX2MEMbuf_1_condo, memreadorwrite_1_oe, memreadorwrite_2_oe,
       memreadorwrite_2_we, or_1_out, stall, xor_1_out;
  wire [4:0] memmappedio_1_screenx, memmappedio_1_screeny;
  wire [11:0] EX2MEMbuf_1_aluouto_2, register_1_q_2;
  wire [14:0] memmappedio_1_screencolor;
  wire [19:0] EX2MEMbuf_1_aluouto, register_1_q;
  wire [20:0] EX2MEMbuf_1_iro, ID2EXbuf_1_iro, irnormalizer_1_normir, MEM2WBbuf_1_iro;
  wire [31:0] adder_1_out, Ainpmux_1_ao, Ainpmux_1_jumpconda, Binpmux_1_bo, Binpmux_1_jumpcondb,
       Binpmux_1_memwrite, EX2MEMbuf_1_writevalo, ID2EXbuf_1_ao, ID2EXbuf_1_bo, ID2EXbuf_1_immo,
       ID2EXbuf_1_npco, IF2IDbuf_1_iro, IF2IDbuf_1_npco, IF2IDbuf_1_pco, irnormalizer_1_signextendimm,
       MEM2WBbuf_1_aluouto, MEM2WBbuf_1_memdatao, multiplexer_1_out, multiplexer_2_out, multiplexer_3_out,
       RAM_1_dout, RAM_2_dout, Regbank32OfEm_1_a, Regbank32OfEm_1_b, riskALU_1_res;

  Multiplexer #(.width(32)) multiplexer_1 (
    .in0(multiplexer_2_out), .in1({register_1_q_2, register_1_q}), .out(multiplexer_1_out), .sel(stall));
  Register #(.width(32)) register_1 (
    .D(multiplexer_1_out), .en(1'b1), .clk(clk), .Q({register_1_q_2, register_1_q}), .clr(Input_2));
  Clock clock_1 (.out(clk));
  or or_1 (or_1_out, \break , clk);
  xor xor_1 (xor_1_out, Input_1, or_1_out);
  RAM #(.addrWidth(20), .dataWidth(32), .trigger("falling")) RAM_1 (
    .addr(register_1_q), .oe(1'b1), .clk(clk), .dout(RAM_1_dout));  // open: we, din
  Adder #(.width(32)) adder_1 (.a(32'h1), .b({register_1_q_2, register_1_q}), .out(adder_1_out));  // open: cin, cout
  Multiplexer #(.width(32)) multiplexer_2 (
    .in0(adder_1_out), .in1({EX2MEMbuf_1_aluouto_2, EX2MEMbuf_1_aluouto}), .out(multiplexer_2_out),
    .sel(EX2MEMbuf_1_condo));
  IF2IDbuf IF2IDbuf_1 (
    .stall(stall), .rst(Input_2), .clk(clk), .IRi(RAM_1_dout), .NPCi(multiplexer_2_out),
    .PCi({register_1_q_2, register_1_q}), .NPCo(IF2IDbuf_1_npco), .PCo(IF2IDbuf_1_pco), .IRo(IF2IDbuf_1_iro));
  IRNormalizer irnormalizer_1 (
    .IR(IF2IDbuf_1_iro), .normIR(irnormalizer_1_normir), .signextendIMM(irnormalizer_1_signextendimm));
  reliesonLoadchecker reliesonLoadchecker_1 (.IF2IDir(irnormalizer_1_normir), .ID2EXir(ID2EXbuf_1_iro), .stall(stall));
  Regbank32OfEm Regbank32OfEm_1 (
    .wbIR(MEM2WBbuf_1_iro), .PC(IF2IDbuf_1_pco), .rst(Input_2), .clk(clk), .wbdata(multiplexer_3_out),
    .IR(irnormalizer_1_normir), .A(Regbank32OfEm_1_a), .B(Regbank32OfEm_1_b));
  ID2EXbuf ID2EXbuf_1 (
    .Immi(irnormalizer_1_signextendimm), .IRi(irnormalizer_1_normir), .NPCi(IF2IDbuf_1_npco), .stall(stall),
    .rst(Input_2), .clk(clk), .Bi(Regbank32OfEm_1_b), .Ai(Regbank32OfEm_1_a), .NPCo(ID2EXbuf_1_npco),
    .Immo(ID2EXbuf_1_immo), .IRo(ID2EXbuf_1_iro), .Ao(ID2EXbuf_1_ao), .Bo(ID2EXbuf_1_bo));
  Ainpmux Ainpmux_1 (
    .A(ID2EXbuf_1_ao), .MEMout(multiplexer_3_out), .NPC(ID2EXbuf_1_npco),
    .EX2MEMalu({EX2MEMbuf_1_aluouto_2, EX2MEMbuf_1_aluouto}), .IR(ID2EXbuf_1_iro),
    .MEM2WBir(MEM2WBbuf_1_iro), .EX2MEMir(EX2MEMbuf_1_iro), .Ao(Ainpmux_1_ao), .jumpcondA(Ainpmux_1_jumpconda));
  Binpmux Binpmux_1 (
    .B(ID2EXbuf_1_bo), .MEMout(multiplexer_3_out), .imm(ID2EXbuf_1_immo),
    .EX2MEMalu({EX2MEMbuf_1_aluouto_2, EX2MEMbuf_1_aluouto}), .IR(ID2EXbuf_1_iro),
    .MEM2WBir(MEM2WBbuf_1_iro), .EX2MEMir(EX2MEMbuf_1_iro), .Bo(Binpmux_1_bo),
    .jumpcondB(Binpmux_1_jumpcondb), .memwrite(Binpmux_1_memwrite));
  riskALU riskALU_1 (.IR(ID2EXbuf_1_iro), .A(Ainpmux_1_ao), .B(Binpmux_1_bo), .res(riskALU_1_res));
  branchCondition branchCondition_1 (
    .IR(ID2EXbuf_1_iro), .A(Ainpmux_1_jumpconda), .B(Binpmux_1_jumpcondb), .jump(branchCondition_1_jump));
  EX2MEMbuf EX2MEMbuf_1 (
    .rst(Input_2), .clk(clk), .aluouti(riskALU_1_res), .writevali(Binpmux_1_memwrite), .IRi(ID2EXbuf_1_iro),
    .condi(branchCondition_1_jump), .aluouto({EX2MEMbuf_1_aluouto_2, EX2MEMbuf_1_aluouto}),
    .writevalo(EX2MEMbuf_1_writevalo), .IRo(EX2MEMbuf_1_iro), .condo(EX2MEMbuf_1_condo));
  memMappedIO memmappedio_1 (
    .addr({EX2MEMbuf_1_aluouto_2, EX2MEMbuf_1_aluouto}), .data(EX2MEMbuf_1_writevalo), .IR(EX2MEMbuf_1_iro),
    .screenx(memmappedio_1_screenx), .screeny(memmappedio_1_screeny),
    .screencolor(memmappedio_1_screencolor), .screenWE(\break ));
  // RGB_Video #(.height(32), .scale(4), .width(32)) rgb_video_1: pin names not known; wires that end beside it: Input_2, clk, \break , memmappedio_1_screenx, memmappedio_1_screeny, memmappedio_1_screencolor
  RAM #(.addrWidth(20), .dataWidth(32), .trigger("falling")) RAM_2 (
    .addr(EX2MEMbuf_1_aluouto), .we(memreadorwrite_2_we), .oe(memreadorwrite_2_oe), .clk(clk),
    .din(EX2MEMbuf_1_writevalo), .dout(RAM_2_dout));
  memreadorwrite memreadorwrite_2 (.IR(EX2MEMbuf_1_iro), .WE(memreadorwrite_2_we), .OE(memreadorwrite_2_oe));
  MEM2WBbuf MEM2WBbuf_1 (
    .rst(Input_2), .clk(clk), .aluouti({EX2MEMbuf_1_aluouto_2, EX2MEMbuf_1_aluouto}), .IRi(EX2MEMbuf_1_iro),
    .memdatai(RAM_2_dout), .aluouto(MEM2WBbuf_1_aluouto), .IRo(MEM2WBbuf_1_iro),
    .memdatao(MEM2WBbuf_1_memdatao));
  Multiplexer #(.width(32)) multiplexer_3 (
    .in0(MEM2WBbuf_1_aluouto), .in1(MEM2WBbuf_1_memdatao), .out(multiplexer_3_out), .sel(memreadorwrite_1_oe));
  memreadorwrite memreadorwrite_1 (.IR(MEM2WBbuf_1_iro), .OE(memreadorwrite_1_oe));  // open: WE

  // Other names for the same wires on the sheet: rst = Input_2

  // Notes on the sheet:
  //   PC
  //   IF
  //   ID/REG
  //   EX
  //   MEM
  //   REGWB
endmodule

module IF2IDbuf (
  input  stall,
  input  rst,
  input  clk,
  input  [31:0] IRi,
  input  [31:0] NPCi,
  input  [31:0] PCi,
  output [31:0] IRo,
  output [31:0] NPCo,
  output [31:0] PCo
);

  wire [31:0] multiplexer_1_out, multiplexer_2_out, multiplexer_3_out;

  Register #(.width(32)) register_1 (.D(multiplexer_1_out), .en(1'b1), .clk(clk), .Q(IRo), .clr(rst));
  Multiplexer #(.width(32)) multiplexer_1 (.in0(IRi), .in1(IRo), .out(multiplexer_1_out), .sel(stall));
  Register #(.width(32)) register_2 (.D(multiplexer_2_out), .en(1'b1), .clk(clk), .Q(NPCo), .clr(rst));
  Multiplexer #(.width(32)) multiplexer_2 (.in0(NPCi), .in1(NPCo), .out(multiplexer_2_out), .sel(stall));
  Register #(.width(32)) register_3 (.D(multiplexer_3_out), .en(1'b1), .clk(clk), .Q(PCo), .clr(rst));
  Multiplexer #(.width(32)) multiplexer_3 (.in0(PCi), .in1(PCo), .out(multiplexer_3_out), .sel(stall));
endmodule

module ID2EXbuf (
  input  stall,
  input  rst,
  input  clk,
  input  [31:0] Ai,
  input  [31:0] Bi,
  input  [31:0] NPCi,
  input  [31:0] Immi,
  input  [20:0] IRi,
  output [31:0] Ao,
  output [31:0] Bo,
  output [31:0] NPCo,
  output [31:0] Immo,
  output [20:0] IRo
);

  wire [20:0] multiplexer_5_out;
  wire [31:0] multiplexer_1_out, multiplexer_2_out, multiplexer_3_out, multiplexer_4_out;

  Multiplexer #(.width(32)) multiplexer_1 (.in0(Ai), .in1({32{1'b0}}), .out(multiplexer_1_out), .sel(stall));
  Multiplexer #(.width(32)) multiplexer_2 (.in0(Bi), .in1({32{1'b0}}), .out(multiplexer_2_out), .sel(stall));
  Multiplexer #(.width(32)) multiplexer_3 (.in0(NPCi), .in1({32{1'b0}}), .out(multiplexer_3_out), .sel(stall));
  Multiplexer #(.width(32)) multiplexer_4 (.in0(Immi), .in1({32{1'b0}}), .out(multiplexer_4_out), .sel(stall));
  Multiplexer #(.width(21)) multiplexer_5 (.in0(IRi), .in1({21{1'b0}}), .out(multiplexer_5_out), .sel(stall));
  Register #(.width(32)) register_1 (.D(multiplexer_1_out), .en(1'b1), .clk(clk), .Q(Ao), .clr(rst));
  Register #(.width(32)) register_2 (.D(multiplexer_2_out), .en(1'b1), .clk(clk), .Q(Bo), .clr(rst));
  Register #(.width(32)) register_3 (.D(multiplexer_3_out), .en(1'b1), .clk(clk), .Q(NPCo), .clr(rst));
  Register #(.width(32)) register_4 (.D(multiplexer_4_out), .en(1'b1), .clk(clk), .Q(Immo), .clr(rst));
  Register #(.width(21)) register_5 (.D(multiplexer_5_out), .en(1'b1), .clk(clk), .Q(IRo), .clr(rst));
endmodule

module EX2MEMbuf (
  input  rst,
  input  clk,
  input  condi,
  input  [31:0] aluouti,
  input  [31:0] writevali,
  input  [20:0] IRi,
  output condo,
  output [31:0] aluouto,
  output [31:0] writevalo,
  output [20:0] IRo
);

  Register #(.width(1)) register_1 (.D(condi), .en(1'b1), .clk(clk), .Q(condo), .clr(rst));
  Register #(.width(32)) register_2 (.D(aluouti), .en(1'b1), .clk(clk), .Q(aluouto), .clr(rst));
  Register #(.width(32)) register_3 (.D(writevali), .en(1'b1), .clk(clk), .Q(writevalo), .clr(rst));
  Register #(.width(21)) register_4 (.D(IRi), .en(1'b1), .clk(clk), .Q(IRo), .clr(rst));
endmodule

module MEM2WBbuf (
  input  rst,
  input  clk,
  input  [31:0] memdatai,
  input  [31:0] aluouti,
  input  [20:0] IRi,
  output [31:0] memdatao,
  output [31:0] aluouto,
  output [20:0] IRo
);

  Register #(.width(32)) register_1 (.D(memdatai), .en(1'b1), .clk(clk), .Q(memdatao), .clr(rst));
  Register #(.width(32)) register_2 (.D(aluouti), .en(1'b1), .clk(clk), .Q(aluouto), .clr(rst));
  Register #(.width(21)) register_3 (.D(IRi), .en(1'b1), .clk(clk), .Q(IRo), .clr(rst));
endmodule

module Regbank32OfEm (
  input  rst,
  input  clk,
  input  [31:0] wbdata,
  input  [20:0] IR,
  input  [20:0] wbIR,
  input  [31:0] PC,
  output [31:0] A,
  output [31:0] B
);

  wire and_1_out, and_2_out, comparator_1_eq, comparator_2_eq, SuperIRdecoder_1_add, SuperIRdecoder_1_adi,
       SuperIRdecoder_1_andd, SuperIRdecoder_1_andi, SuperIRdecoder_1_jal, SuperIRdecoder_1_jalr,
       SuperIRdecoder_1_li, SuperIRdecoder_1_lw, SuperIRdecoder_1_mv, SuperIRdecoder_1_neg,
       SuperIRdecoder_1_nott, SuperIRdecoder_1_ori, SuperIRdecoder_1_orr, SuperIRdecoder_1_slli,
       SuperIRdecoder_1_slll, SuperIRdecoder_1_sraa, SuperIRdecoder_1_srai, SuperIRdecoder_1_srli,
       SuperIRdecoder_1_srll, SuperIRdecoder_1_sub, w1, w2, w3, w4, w5, w6, w7, w8, w9, w10, w11, w12, w13,
       w14, w15, w16, w17, w18, w19, w20, w21, w22, w23, w24, w25, w26, w27, w28, w29, w30, w31, w32, wbEN;
  wire [4:0] IRsplitter_1_rs1, IRsplitter_1_rs2, IRsplitter_2_rd;
  wire [5:0] IRsplitter_2_opcode;
  wire [31:0] multiplexer_1_out, multiplexer_2_out, o3, o4, o5, o6, o7, o8, o9, o10, o11, o12, o13, o14, o15,
       o16, o17, o18, o19, o20, o21, o22, o23, o24, o25, o26, o27, o28, o29, o30, o31;

  Decoder #(.select(5)) decoder_1 (
    .out0(w1), .out1(w2), .out2(w3), .out3(w4), .out4(w5), .out5(w6), .out6(w7), .out7(w8), .out8(w9),
    .out9(w10), .out10(w11), .out11(w12), .out12(w13), .out13(w14), .out14(w15), .out15(w16), .out16(w17),
    .out17(w18), .out18(w19), .out19(w20), .out20(w21), .out21(w22), .out22(w23), .out23(w24), .out24(w25),
    .out25(w26), .out26(w27), .out27(w28), .out28(w29), .out29(w30), .out30(w31), .out31(w32),
    .sel(IRsplitter_2_rd), .en(wbEN));
  IRsplitter IRsplitter_2 (.IR(wbIR), .rd(IRsplitter_2_rd), .opcode(IRsplitter_2_opcode));  // open: rs2, rs1
  SuperIRdecoder SuperIRdecoder_1 (
    .opcode(IRsplitter_2_opcode), .sub(SuperIRdecoder_1_sub), .andi(SuperIRdecoder_1_andi),
    .ori(SuperIRdecoder_1_ori), .slli(SuperIRdecoder_1_slli), .srli(SuperIRdecoder_1_srli),
    .srai(SuperIRdecoder_1_srai), .lw(SuperIRdecoder_1_lw), .jalr(SuperIRdecoder_1_jalr),
    .li(SuperIRdecoder_1_li), .adi(SuperIRdecoder_1_adi), .add(SuperIRdecoder_1_add),
    .neg(SuperIRdecoder_1_neg), .andd(SuperIRdecoder_1_andd), .orr(SuperIRdecoder_1_orr),
    .slll(SuperIRdecoder_1_slll), .srll(SuperIRdecoder_1_srll), .sraa(SuperIRdecoder_1_sraa),
    .jal(SuperIRdecoder_1_jal), .nott(SuperIRdecoder_1_nott), .mv(SuperIRdecoder_1_mv));  // open: j, beq, blt, bge, nop, sw, bne, bgt, ble, jr
  or or_1 (wbEN, SuperIRdecoder_1_slli, SuperIRdecoder_1_nott, SuperIRdecoder_1_adi, SuperIRdecoder_1_add, SuperIRdecoder_1_sub, SuperIRdecoder_1_neg, SuperIRdecoder_1_andi, SuperIRdecoder_1_andd, SuperIRdecoder_1_ori, SuperIRdecoder_1_orr, SuperIRdecoder_1_slll, SuperIRdecoder_1_srli, SuperIRdecoder_1_srll, SuperIRdecoder_1_srai, SuperIRdecoder_1_sraa, SuperIRdecoder_1_jal, SuperIRdecoder_1_lw, SuperIRdecoder_1_jalr, SuperIRdecoder_1_li, SuperIRdecoder_1_mv);
  IRsplitter IRsplitter_1 (.IR(IR), .rs2(IRsplitter_1_rs2), .rs1(IRsplitter_1_rs1));  // open: rd, opcode
  Multiplexer #(.select(5), .width(32)) multiplexer_1 (
    .in0({32{1'b0}}), .in1(32'h1), .in2(o3), .in3(o4), .in4(o5), .in5(o6), .in6(o7), .in7(o8), .in8(o9),
    .in9(o10), .in10(o11), .in11(o12), .in12(o13), .in13(o14), .in14(o15), .in15(o16), .in16(o17),
    .in17(o18), .in18(o19), .in19(o20), .in20(o21), .in21(o22), .in22(o23), .in23(o24), .in24(o25),
    .in25(o26), .in26(o27), .in27(o28), .in28(o29), .in29(o30), .in30(o31), .in31(PC),
    .out(multiplexer_1_out), .sel(IRsplitter_1_rs1));
  Multiplexer #(.select(5), .width(32)) multiplexer_2 (
    .in0({32{1'b0}}), .in1(32'h1), .in2(o3), .in3(o4), .in4(o5), .in5(o6), .in6(o7), .in7(o8), .in8(o9),
    .in9(o10), .in10(o11), .in11(o12), .in12(o13), .in13(o14), .in14(o15), .in15(o16), .in16(o17),
    .in17(o18), .in18(o19), .in19(o20), .in20(o21), .in21(o22), .in22(o23), .in23(o24), .in24(o25),
    .in25(o26), .in26(o27), .in27(o28), .in28(o29), .in29(o30), .in30(o31), .in31(PC),
    .out(multiplexer_2_out), .sel(IRsplitter_1_rs2));
  Comparator #(.width(5)) comparator_1 (
    .a(IRsplitter_1_rs2), .b(IRsplitter_2_rd), .eq(comparator_1_eq));  // open: gt, lt
  Comparator #(.width(5)) comparator_2 (
    .a(IRsplitter_2_rd), .b(IRsplitter_1_rs1), .eq(comparator_2_eq));  // open: gt, lt
  and and_1 (and_1_out, comparator_1_eq, wbEN);
  Multiplexer #(.width(32)) multiplexer_3 (.in0(multiplexer_1_out), .in1(wbdata), .out(A), .sel(and_2_out));
  and and_2 (and_2_out, comparator_2_eq, wbEN);
  Multiplexer #(.width(32)) multiplexer_4 (.in0(multiplexer_2_out), .in1(wbdata), .out(B), .sel(and_1_out));
  Register #(.width(32)) register_1 (.D(wbdata), .en(w5), .clk(clk), .Q(o5), .clr(rst));
  Register #(.width(32)) register_2 (.D(wbdata), .en(w9), .clk(clk), .Q(o9), .clr(rst));
  Register #(.width(32)) register_3 (.D(wbdata), .en(w13), .clk(clk), .Q(o13), .clr(rst));
  Register #(.width(32)) register_4 (.D(wbdata), .en(w17), .clk(clk), .Q(o17), .clr(rst));
  Register #(.width(32)) register_5 (.D(wbdata), .en(w21), .clk(clk), .Q(o21), .clr(rst));
  Register #(.width(32)) register_6 (.D(wbdata), .en(w25), .clk(clk), .Q(o25), .clr(rst));
  Register #(.width(32)) register_7 (.D(wbdata), .en(w29), .clk(clk), .Q(o29), .clr(rst));
  Register #(.width(32)) register_8 (.D(wbdata), .en(w6), .clk(clk), .Q(o6), .clr(rst));
  Register #(.width(32)) register_9 (.D(wbdata), .en(w10), .clk(clk), .Q(o10), .clr(rst));
  Register #(.width(32)) register_10 (.D(wbdata), .en(w14), .clk(clk), .Q(o14), .clr(rst));
  Register #(.width(32)) register_11 (.D(wbdata), .en(w18), .clk(clk), .Q(o18), .clr(rst));
  Register #(.width(32)) register_12 (.D(wbdata), .en(w22), .clk(clk), .Q(o22), .clr(rst));
  Register #(.width(32)) register_13 (.D(wbdata), .en(w26), .clk(clk), .Q(o26), .clr(rst));
  Register #(.width(32)) register_14 (.D(wbdata), .en(w30), .clk(clk), .Q(o30), .clr(rst));
  Register #(.width(32)) register_15 (.D(wbdata), .en(w3), .clk(clk), .Q(o3), .clr(rst));
  Register #(.width(32)) register_16 (.D(wbdata), .en(w7), .clk(clk), .Q(o7), .clr(rst));
  Register #(.width(32)) register_17 (.D(wbdata), .en(w11), .clk(clk), .Q(o11), .clr(rst));
  Register #(.width(32)) register_18 (.D(wbdata), .en(w15), .clk(clk), .Q(o15), .clr(rst));
  Register #(.width(32)) register_19 (.D(wbdata), .en(w19), .clk(clk), .Q(o19), .clr(rst));
  Register #(.width(32)) register_20 (.D(wbdata), .en(w23), .clk(clk), .Q(o23), .clr(rst));
  Register #(.width(32)) register_21 (.D(wbdata), .en(w27), .clk(clk), .Q(o27), .clr(rst));
  Register #(.width(32)) register_22 (.D(wbdata), .en(w31), .clk(clk), .Q(o31), .clr(rst));
  Register #(.width(32)) register_23 (.D(wbdata), .en(w4), .clk(clk), .Q(o4), .clr(rst));
  Register #(.width(32)) register_24 (.D(wbdata), .en(w8), .clk(clk), .Q(o8), .clr(rst));
  Register #(.width(32)) register_25 (.D(wbdata), .en(w12), .clk(clk), .Q(o12), .clr(rst));
  Register #(.width(32)) register_26 (.D(wbdata), .en(w16), .clk(clk), .Q(o16), .clr(rst));
  Register #(.width(32)) register_27 (.D(wbdata), .en(w20), .clk(clk), .Q(o20), .clr(rst));
  Register #(.width(32)) register_28 (.D(wbdata), .en(w24), .clk(clk), .Q(o24), .clr(rst));
  Register #(.width(32)) register_29 (.D(wbdata), .en(w28), .clk(clk), .Q(o28), .clr(rst));

  // Other names for the same wires on the sheet: o32[31:0] = PC; wb[31:0] = wbdata

  // Notes on the sheet:
  //   x0 constant 0
  //   ARG
  //   x1 constant 1
  //   LCL
  //   PTR2
  //   SP
  //   PTR1
endmodule

module SuperIRdecoder (
  input  [5:0] opcode,
  output nop,
  output sw,
  output li,
  output mv,
  output adi,
  output add,
  output sub,
  output neg,
  output andi,
  output andd,
  output ori,
  output orr,
  output slli,
  output slll,
  output srli,
  output srll,
  output srai,
  output sraa,
  output j,
  output jal,
  output beq,
  output bne,
  output blt,
  output bgt,
  output bge,
  output ble,
  output lw,
  output jr,
  output jalr,
  output nott
);

  wire not_1_out;

  Decoder #(.select(5)) decoder_1 (
    .out0(nop), .out2(sw), .out4(li), .out5(mv), .out6(adi), .out7(add), .out8(sub), .out9(neg),
    .out10(andi), .out11(andd), .out12(ori), .out13(orr), .out14(slli), .out15(slll), .out16(srli),
    .out17(srll), .out18(srai), .out19(sraa), .out20(j), .out21(jal), .out22(beq), .out23(bne), .out24(blt),
    .out25(bgt), .out26(bge), .out27(ble), .out28(lw), .out29(jr), .out30(jalr), .out31(nott),
    .sel(opcode[4:0]), .en(not_1_out));  // open: out1, out3
  not not_1 (not_1_out, opcode[5]);

  // Notes on the sheet:
  //   lb
  //   sb
  //   and
  //   or
  //   sll
  //   srl
  //   sra
  //   not
endmodule

module IRsplitter (
  input  [20:0] IR,
  output [5:0] opcode,
  output [4:0] rs2,
  output [4:0] rs1,
  output [4:0] rd
);


  assign opcode = IR[5:0];
  assign rd = IR[20:16];
  assign rs1 = IR[15:11];
  assign rs2 = IR[10:6];
endmodule

module IRbranchchecker (
  input  [20:0] IR,
  output branchop
);

  wire SuperIRdecoder_1_beq, SuperIRdecoder_1_bge, SuperIRdecoder_1_bgt, SuperIRdecoder_1_ble,
       SuperIRdecoder_1_blt, SuperIRdecoder_1_bne, SuperIRdecoder_1_j;
  wire [5:0] IRsplitter_1_opcode;

  IRsplitter IRsplitter_1 (.IR(IR), .opcode(IRsplitter_1_opcode));  // open: rs2, rd, rs1
  SuperIRdecoder SuperIRdecoder_1 (
    .opcode(IRsplitter_1_opcode), .j(SuperIRdecoder_1_j), .beq(SuperIRdecoder_1_beq),
    .blt(SuperIRdecoder_1_blt), .bge(SuperIRdecoder_1_bge), .bne(SuperIRdecoder_1_bne),
    .bgt(SuperIRdecoder_1_bgt), .ble(SuperIRdecoder_1_ble));  // open: sub, andi, ori, slli, srli, srai, lw, jalr, nop, sw, li, adi, add, neg, andd, orr, slll, srll, sraa, jal, jr, nott, mv
  or or_1 (branchop, SuperIRdecoder_1_j, SuperIRdecoder_1_beq, SuperIRdecoder_1_bne, SuperIRdecoder_1_blt, SuperIRdecoder_1_bgt, SuperIRdecoder_1_bge, SuperIRdecoder_1_ble);
endmodule

module immRDmaker (
  input  [20:0] IR,
  output [31:0] imm
);

  wire or_1_out, SuperIRdecoder_1_beq, SuperIRdecoder_1_bge, SuperIRdecoder_1_bgt, SuperIRdecoder_1_ble,
       SuperIRdecoder_1_blt, SuperIRdecoder_1_bne, SuperIRdecoder_1_j;
  wire [4:0] IRsplitter_1_p3;
  wire [5:0] IRsplitter_1_p2;
  wire [10:0] IRsplitter_1_p4;
  wire [31:0] bit_extender_1_out, bit_extender_2_out;

  // IRsplitter IRsplitter_1: pin names not known; wires that end beside it: IR, IRsplitter_1_p2, IRsplitter_1_p3, IRsplitter_1_p4
  SuperIRdecoder SuperIRdecoder_1 (
    .opcode(IRsplitter_1_p2), .j(SuperIRdecoder_1_j), .beq(SuperIRdecoder_1_beq), .blt(SuperIRdecoder_1_blt),
    .bge(SuperIRdecoder_1_bge), .bne(SuperIRdecoder_1_bne), .bgt(SuperIRdecoder_1_bgt),
    .ble(SuperIRdecoder_1_ble));  // open: sub, andi, ori, slli, srli, srai, lw, jalr, nop, sw, li, adi, add, neg, andd, orr, slll, srll, sraa, jal, jr, nott, mv
  assign bit_extender_1_out = {{16{IRsplitter_1_p4[10]}}, {IRsplitter_1_p4, IRsplitter_1_p3}};  // Bit_Extender bit_extender_1
  assign bit_extender_2_out = {{21{IRsplitter_1_p4[10]}}, IRsplitter_1_p4};  // Bit_Extender bit_extender_2
  or or_1 (or_1_out, SuperIRdecoder_1_j, SuperIRdecoder_1_beq, SuperIRdecoder_1_bne, SuperIRdecoder_1_blt, SuperIRdecoder_1_bgt, SuperIRdecoder_1_bge, SuperIRdecoder_1_ble);
  Multiplexer #(.width(32)) multiplexer_1 (
    .in0(bit_extender_2_out), .in1(bit_extender_1_out), .out(imm), .sel(or_1_out));

  // Notes on the sheet:
  //   concatanate imm and RD if needed
  //   need immRD
endmodule

module IRimmchecker (
  input  [20:0] IR,
  output needimm
);

  wire SuperIRdecoder_1_adi, SuperIRdecoder_1_andi, SuperIRdecoder_1_beq, SuperIRdecoder_1_bge,
       SuperIRdecoder_1_bgt, SuperIRdecoder_1_ble, SuperIRdecoder_1_blt, SuperIRdecoder_1_bne,
       SuperIRdecoder_1_j, SuperIRdecoder_1_li, SuperIRdecoder_1_lw, SuperIRdecoder_1_ori,
       SuperIRdecoder_1_slli, SuperIRdecoder_1_srai, SuperIRdecoder_1_srli, SuperIRdecoder_1_sw;
  wire [5:0] IRsplitter_1_opcode;

  IRsplitter IRsplitter_1 (.IR(IR), .opcode(IRsplitter_1_opcode));  // open: rs2, rd, rs1
  SuperIRdecoder SuperIRdecoder_1 (
    .opcode(IRsplitter_1_opcode), .andi(SuperIRdecoder_1_andi), .ori(SuperIRdecoder_1_ori),
    .slli(SuperIRdecoder_1_slli), .srli(SuperIRdecoder_1_srli), .srai(SuperIRdecoder_1_srai),
    .j(SuperIRdecoder_1_j), .beq(SuperIRdecoder_1_beq), .blt(SuperIRdecoder_1_blt),
    .bge(SuperIRdecoder_1_bge), .lw(SuperIRdecoder_1_lw), .sw(SuperIRdecoder_1_sw), .li(SuperIRdecoder_1_li),
    .adi(SuperIRdecoder_1_adi), .bne(SuperIRdecoder_1_bne), .bgt(SuperIRdecoder_1_bgt),
    .ble(SuperIRdecoder_1_ble));  // open: sub, jalr, nop, add, neg, andd, orr, slll, srll, sraa, jal, jr, nott, mv
  or or_1 (needimm, SuperIRdecoder_1_sw, SuperIRdecoder_1_adi, SuperIRdecoder_1_andi, SuperIRdecoder_1_ori, SuperIRdecoder_1_slli, SuperIRdecoder_1_srli, SuperIRdecoder_1_srai, SuperIRdecoder_1_j, SuperIRdecoder_1_beq, SuperIRdecoder_1_bne, SuperIRdecoder_1_blt, SuperIRdecoder_1_bgt, SuperIRdecoder_1_bge, SuperIRdecoder_1_ble, SuperIRdecoder_1_lw, SuperIRdecoder_1_li);
endmodule

module riskALU (
  input  [20:0] IR,
  input  [31:0] A,
  input  [31:0] B,
  output [31:0] res
);

  wire andd, bigAdder, li, neg, negator, orr, passA, sllogic, srarith, srlogic, SuperIRdecoder_1_add,
       SuperIRdecoder_1_adi, SuperIRdecoder_1_andd, SuperIRdecoder_1_andi, SuperIRdecoder_1_beq,
       SuperIRdecoder_1_bge, SuperIRdecoder_1_bgt, SuperIRdecoder_1_ble, SuperIRdecoder_1_blt,
       SuperIRdecoder_1_bne, SuperIRdecoder_1_j, SuperIRdecoder_1_jr, SuperIRdecoder_1_lw,
       SuperIRdecoder_1_mv, SuperIRdecoder_1_nott, SuperIRdecoder_1_ori, SuperIRdecoder_1_orr,
       SuperIRdecoder_1_slli, SuperIRdecoder_1_slll, SuperIRdecoder_1_sraa, SuperIRdecoder_1_srai,
       SuperIRdecoder_1_srli, SuperIRdecoder_1_srll, SuperIRdecoder_1_sub, SuperIRdecoder_1_sw;
  wire [5:0] IRsplitter_1_opcode;
  wire [31:0] adder_1_out, AddSub32Bit_1_y, and_1_out, multiplexer_2_out, multiplexer_3_out,
       multiplexer_4_out, multiplexer_5_out, multiplexer_6_out, multiplexer_7_out, multiplexer_8_out,
       multiplexer_9_out, not_1_out, or_3_out, shifter_1_out, shifter_2_out, shifter_3_out;

  IRsplitter IRsplitter_1 (.IR(IR), .opcode(IRsplitter_1_opcode));  // open: rs2, rd, rs1
  SuperIRdecoder SuperIRdecoder_1 (
    .opcode(IRsplitter_1_opcode), .sub(SuperIRdecoder_1_sub), .andi(SuperIRdecoder_1_andi),
    .ori(SuperIRdecoder_1_ori), .slli(SuperIRdecoder_1_slli), .srli(SuperIRdecoder_1_srli),
    .srai(SuperIRdecoder_1_srai), .j(SuperIRdecoder_1_j), .beq(SuperIRdecoder_1_beq),
    .blt(SuperIRdecoder_1_blt), .bge(SuperIRdecoder_1_bge), .lw(SuperIRdecoder_1_lw),
    .sw(SuperIRdecoder_1_sw), .li(li), .adi(SuperIRdecoder_1_adi), .add(SuperIRdecoder_1_add), .neg(neg),
    .andd(SuperIRdecoder_1_andd), .orr(SuperIRdecoder_1_orr), .slll(SuperIRdecoder_1_slll),
    .srll(SuperIRdecoder_1_srll), .sraa(SuperIRdecoder_1_sraa), .bne(SuperIRdecoder_1_bne),
    .bgt(SuperIRdecoder_1_bgt), .ble(SuperIRdecoder_1_ble), .jr(SuperIRdecoder_1_jr),
    .nott(SuperIRdecoder_1_nott), .mv(SuperIRdecoder_1_mv));  // open: jalr, nop, jal
  or or_1 (bigAdder, SuperIRdecoder_1_j, SuperIRdecoder_1_beq, SuperIRdecoder_1_bne, SuperIRdecoder_1_blt, SuperIRdecoder_1_sw, SuperIRdecoder_1_adi, SuperIRdecoder_1_add, SuperIRdecoder_1_sub, SuperIRdecoder_1_lw, SuperIRdecoder_1_bgt, SuperIRdecoder_1_bge, SuperIRdecoder_1_ble);
  or or_2 (negator, neg, SuperIRdecoder_1_nott);
  AddSub32Bit AddSub32Bit_1 (.B(B), .A(A), .Input_1(SuperIRdecoder_1_sub), .Y(AddSub32Bit_1_y));  // open: Overflow
  assign not_1_out = ~A;  // NOT_Gate not_1, 32 bits wide
  Adder #(.width(32)) adder_1 (.a({32{1'b0}}), .b(not_1_out), .out(adder_1_out), .cin(neg));  // open: cout
  assign and_1_out = A & B;  // AND_Gate and_1, 32 bits wide
  assign or_3_out = A | B;  // OR_Gate or_3, 32 bits wide
  Shifter #(.width(32)) shifter_1 (.in(A), .\dist (B[4:0]), .out(shifter_1_out));
  Shifter #(.shift("lr"), .width(32)) shifter_2 (.in(A), .\dist (B[4:0]), .out(shifter_2_out));
  Shifter #(.shift("ar"), .width(32)) shifter_3 (.in(A), .\dist (B[4:0]), .out(shifter_3_out));
  or or_4 (andd, SuperIRdecoder_1_andi, SuperIRdecoder_1_andd);
  or or_5 (orr, SuperIRdecoder_1_ori, SuperIRdecoder_1_orr);
  or or_6 (sllogic, SuperIRdecoder_1_slli, SuperIRdecoder_1_slll);
  Multiplexer #(.width(32)) multiplexer_1 (.in0(multiplexer_2_out), .in1(AddSub32Bit_1_y), .out(res), .sel(bigAdder));
  Multiplexer #(.width(32)) multiplexer_2 (
    .in0(multiplexer_3_out), .in1(adder_1_out), .out(multiplexer_2_out), .sel(negator));
  Multiplexer #(.width(32)) multiplexer_3 (
    .in0(multiplexer_4_out), .in1(and_1_out), .out(multiplexer_3_out), .sel(andd));
  Multiplexer #(.width(32)) multiplexer_4 (.in0(multiplexer_5_out), .in1(or_3_out), .out(multiplexer_4_out), .sel(orr));
  Multiplexer #(.width(32)) multiplexer_5 (
    .in0(multiplexer_6_out), .in1(shifter_1_out), .out(multiplexer_5_out), .sel(sllogic));
  Multiplexer #(.width(32)) multiplexer_6 (
    .in0(multiplexer_7_out), .in1(shifter_2_out), .out(multiplexer_6_out), .sel(srlogic));
  Multiplexer #(.width(32)) multiplexer_7 (
    .in0(multiplexer_8_out), .in1(shifter_3_out), .out(multiplexer_7_out), .sel(srarith));
  Multiplexer #(.width(32)) multiplexer_8 (.in0(multiplexer_9_out), .in1(B), .out(multiplexer_8_out), .sel(li));
  Multiplexer #(.width(32)) multiplexer_9 (.in0({32{1'b0}}), .in1(A), .out(multiplexer_9_out), .sel(passA));
  or or_7 (srlogic, SuperIRdecoder_1_srli, SuperIRdecoder_1_srll);
  or or_8 (srarith, SuperIRdecoder_1_srai, SuperIRdecoder_1_sraa);
  or or_9 (passA, SuperIRdecoder_1_jr, SuperIRdecoder_1_mv);

  // Notes on the sheet:
  //   ALU
  //   sw,adi,add,sub,lw,j,branches
  //   neg,not
  //   adi,add
  //   ori,or
  //   slli,sll
  //   srli,srl
  //   srai,sra
  //   mv
  //   li
endmodule

module branchCondition (
  input  [20:0] IR,
  input  [31:0] A,
  input  [31:0] B,
  output jump
);

  wire and_1_out, and_2_out, and_3_out, and_4_out, comparator_1_eq, comparator_1_gt, comparator_1_lt,
       not_1_out, or_1_out, or_2_out, or_3_out, SuperIRdecoder_1_beq, SuperIRdecoder_1_bge,
       SuperIRdecoder_1_bgt, SuperIRdecoder_1_ble, SuperIRdecoder_1_blt, SuperIRdecoder_1_bne,
       SuperIRdecoder_1_j, SuperIRdecoder_1_jr;
  wire [5:0] IRsplitter_1_opcode;

  IRsplitter IRsplitter_1 (.IR(IR), .opcode(IRsplitter_1_opcode));  // open: rs2, rd, rs1
  SuperIRdecoder SuperIRdecoder_1 (
    .opcode(IRsplitter_1_opcode), .j(SuperIRdecoder_1_j), .beq(SuperIRdecoder_1_beq),
    .blt(SuperIRdecoder_1_blt), .bge(SuperIRdecoder_1_bge), .bne(SuperIRdecoder_1_bne),
    .bgt(SuperIRdecoder_1_bgt), .ble(SuperIRdecoder_1_ble), .jr(SuperIRdecoder_1_jr));  // open: sub, andi, ori, slli, srli, srai, lw, jalr, nop, sw, li, adi, add, neg, andd, orr, slll, srll, sraa, jal, nott, mv
  Comparator #(.width(32)) comparator_1 (
    .a(A), .b(B), .gt(comparator_1_gt), .eq(comparator_1_eq), .lt(comparator_1_lt));
  or or_1 (or_1_out, SuperIRdecoder_1_beq, SuperIRdecoder_1_bge, SuperIRdecoder_1_ble);
  not not_1 (not_1_out, comparator_1_eq);
  or or_2 (or_2_out, SuperIRdecoder_1_ble, comparator_1_lt);
  or or_3 (or_3_out, comparator_1_gt, SuperIRdecoder_1_bge);
  and and_1 (and_1_out, or_1_out, comparator_1_eq);
  and and_2 (and_2_out, SuperIRdecoder_1_bne, not_1_out);
  and and_3 (and_3_out, SuperIRdecoder_1_blt, or_2_out);
  and and_4 (and_4_out, SuperIRdecoder_1_bgt, or_3_out);
  or or_4 (jump, SuperIRdecoder_1_j, and_1_out, and_2_out, and_3_out, and_4_out, SuperIRdecoder_1_jr);
endmodule

module memreadorwrite (
  input  [20:0] IR,
  output WE,
  output OE
);

  wire [5:0] IRsplitter_1_opcode;

  IRsplitter IRsplitter_1 (.IR(IR), .opcode(IRsplitter_1_opcode));  // open: rs2, rd, rs1
  SuperIRdecoder SuperIRdecoder_1 (
    .opcode(IRsplitter_1_opcode), .lw(OE), .sw(WE));  // open: sub, andi, ori, slli, srli, srai, j, beq, blt, bge, jalr, nop, li, adi, add, neg, andd, orr, slll, srll, sraa, jal, bne, bgt, ble, jr, nott, mv
endmodule

module Ainpmux (
  input  [20:0] IR,
  input  [31:0] NPC,
  input  [31:0] EX2MEMalu,
  input  [20:0] EX2MEMir,
  input  [31:0] A,
  input  [31:0] MEMout,
  input  [20:0] MEM2WBir,
  output [31:0] Ao,
  output [31:0] jumpcondA
);

  wire and_1_out, and_2_out, comparator_1_eq, comparator_2_eq, IRbranchchecker_1_branchop,
       opcodeNeedsRS1check_1_needsrs1, writestoRDcheck_1_wrote, writestoRDcheck_2_wrote;
  wire [4:0] IRsplitter_1_rs1, IRsplitter_2_rd, IRsplitter_3_rd;
  wire [5:0] IRsplitter_1_opcode, IRsplitter_2_opcode, IRsplitter_3_opcode;
  wire [31:0] multiplexer_3_out;

  IRsplitter IRsplitter_1 (.IR(IR), .opcode(IRsplitter_1_opcode), .rs1(IRsplitter_1_rs1));  // open: rs2, rd
  IRsplitter IRsplitter_2 (.IR(EX2MEMir), .rd(IRsplitter_2_rd), .opcode(IRsplitter_2_opcode));  // open: rs2, rs1
  IRsplitter IRsplitter_3 (.IR(MEM2WBir), .rd(IRsplitter_3_rd), .opcode(IRsplitter_3_opcode));  // open: rs2, rs1
  opcodeNeedsRS1check opcodeNeedsRS1check_1 (.opcode(IRsplitter_1_opcode), .needsrs1(opcodeNeedsRS1check_1_needsrs1));
  writestoRDcheck writestoRDcheck_1 (.op(IRsplitter_2_opcode), .wrote(writestoRDcheck_1_wrote));  // open: wasload
  writestoRDcheck writestoRDcheck_2 (.op(IRsplitter_3_opcode), .wrote(writestoRDcheck_2_wrote));  // open: wasload
  IRbranchchecker IRbranchchecker_1 (.IR(IR), .branchop(IRbranchchecker_1_branchop));
  Comparator #(.width(5)) comparator_1 (
    .a(IRsplitter_1_rs1), .b(IRsplitter_2_rd), .eq(comparator_1_eq));  // open: gt, lt
  Comparator #(.width(5)) comparator_2 (
    .a(IRsplitter_1_rs1), .b(IRsplitter_3_rd), .eq(comparator_2_eq));  // open: gt, lt
  and and_1 (and_1_out, opcodeNeedsRS1check_1_needsrs1, comparator_1_eq, writestoRDcheck_1_wrote);
  and and_2 (and_2_out, opcodeNeedsRS1check_1_needsrs1, writestoRDcheck_2_wrote, comparator_2_eq);
  Multiplexer #(.width(32)) multiplexer_1 (.in0(jumpcondA), .in1(NPC), .out(Ao), .sel(IRbranchchecker_1_branchop));
  Multiplexer #(.width(32)) multiplexer_2 (.in0(multiplexer_3_out), .in1(EX2MEMalu), .out(jumpcondA), .sel(and_1_out));
  Multiplexer #(.width(32)) multiplexer_3 (.in0(A), .in1(MEMout), .out(multiplexer_3_out), .sel(and_2_out));

  // Notes on the sheet:
  //   needs rd early
  //   needs rd early
endmodule

module Binpmux (
  input  [20:0] IR,
  input  [31:0] imm,
  input  [31:0] EX2MEMalu,
  input  [20:0] EX2MEMir,
  input  [31:0] B,
  input  [31:0] MEMout,
  input  [20:0] MEM2WBir,
  output [31:0] Bo,
  output [31:0] jumpcondB,
  output [31:0] memwrite
);

  wire and_1_out, and_2_out, comparator_1_eq, comparator_2_eq, IRimmchecker_1_needimm,
       opcodeNeedsRS2check_1_needsrs2, writestoRDcheck_1_wrote, writestoRDcheck_2_wrote;
  wire [4:0] IRsplitter_1_rs2, IRsplitter_2_rd, IRsplitter_3_rd;
  wire [5:0] IRsplitter_1_opcode, IRsplitter_2_opcode, IRsplitter_3_opcode;
  wire [31:0] multiplexer_3_out;

  IRsplitter IRsplitter_1 (.IR(IR), .rs2(IRsplitter_1_rs2), .opcode(IRsplitter_1_opcode));  // open: rd, rs1
  IRsplitter IRsplitter_2 (.IR(EX2MEMir), .rd(IRsplitter_2_rd), .opcode(IRsplitter_2_opcode));  // open: rs2, rs1
  IRsplitter IRsplitter_3 (.IR(MEM2WBir), .rd(IRsplitter_3_rd), .opcode(IRsplitter_3_opcode));  // open: rs2, rs1
  opcodeNeedsRS2check opcodeNeedsRS2check_1 (.op(IRsplitter_1_opcode), .needsrs2(opcodeNeedsRS2check_1_needsrs2));
  writestoRDcheck writestoRDcheck_1 (.op(IRsplitter_2_opcode), .wrote(writestoRDcheck_1_wrote));  // open: wasload
  writestoRDcheck writestoRDcheck_2 (.op(IRsplitter_3_opcode), .wrote(writestoRDcheck_2_wrote));  // open: wasload
  IRimmchecker IRimmchecker_1 (.IR(IR), .needimm(IRimmchecker_1_needimm));
  Comparator #(.width(5)) comparator_1 (
    .a(IRsplitter_1_rs2), .b(IRsplitter_2_rd), .eq(comparator_1_eq));  // open: gt, lt
  Comparator #(.width(5)) comparator_2 (
    .a(IRsplitter_1_rs2), .b(IRsplitter_3_rd), .eq(comparator_2_eq));  // open: gt, lt
  and and_1 (and_1_out, opcodeNeedsRS2check_1_needsrs2, comparator_1_eq, writestoRDcheck_1_wrote);
  and and_2 (and_2_out, opcodeNeedsRS2check_1_needsrs2, writestoRDcheck_2_wrote, comparator_2_eq);
  Multiplexer #(.width(32)) multiplexer_1 (.in0(jumpcondB), .in1(imm), .out(Bo), .sel(IRimmchecker_1_needimm));
  Multiplexer #(.width(32)) multiplexer_2 (.in0(multiplexer_3_out), .in1(EX2MEMalu), .out(jumpcondB), .sel(and_1_out));
  Multiplexer #(.width(32)) multiplexer_3 (.in0(B), .in1(MEMout), .out(multiplexer_3_out), .sel(and_2_out));

  assign memwrite = jumpcondB;

  // Notes on the sheet:
  //   needs rd early
  //   needs rd early
endmodule

module writestoRDcheck (
  input  [5:0] op,
  output wrote,
  output wasload
);

  wire SuperIRdecoder_1_add, SuperIRdecoder_1_adi, SuperIRdecoder_1_andd, SuperIRdecoder_1_andi,
       SuperIRdecoder_1_li, SuperIRdecoder_1_mv, SuperIRdecoder_1_neg, SuperIRdecoder_1_nott,
       SuperIRdecoder_1_ori, SuperIRdecoder_1_orr, SuperIRdecoder_1_slli, SuperIRdecoder_1_slll,
       SuperIRdecoder_1_sraa, SuperIRdecoder_1_srai, SuperIRdecoder_1_srli, SuperIRdecoder_1_srll,
       SuperIRdecoder_1_sub, SuperIRdecoder_1_sw;

  SuperIRdecoder SuperIRdecoder_1 (
    .opcode(op), .sub(SuperIRdecoder_1_sub), .andi(SuperIRdecoder_1_andi), .ori(SuperIRdecoder_1_ori),
    .slli(SuperIRdecoder_1_slli), .srli(SuperIRdecoder_1_srli), .srai(SuperIRdecoder_1_srai), .lw(wasload),
    .sw(SuperIRdecoder_1_sw), .li(SuperIRdecoder_1_li), .adi(SuperIRdecoder_1_adi),
    .add(SuperIRdecoder_1_add), .neg(SuperIRdecoder_1_neg), .andd(SuperIRdecoder_1_andd),
    .orr(SuperIRdecoder_1_orr), .slll(SuperIRdecoder_1_slll), .srll(SuperIRdecoder_1_srll),
    .sraa(SuperIRdecoder_1_sraa), .nott(SuperIRdecoder_1_nott), .mv(SuperIRdecoder_1_mv));  // open: j, beq, blt, bge, jalr, nop, jal, bne, bgt, ble, jr
  or or_1 (wrote, SuperIRdecoder_1_sw, SuperIRdecoder_1_adi, SuperIRdecoder_1_add, SuperIRdecoder_1_sub, SuperIRdecoder_1_neg, SuperIRdecoder_1_andi, SuperIRdecoder_1_andd, SuperIRdecoder_1_ori, SuperIRdecoder_1_orr, SuperIRdecoder_1_slli, SuperIRdecoder_1_slll, SuperIRdecoder_1_srli, SuperIRdecoder_1_srll, SuperIRdecoder_1_srai, SuperIRdecoder_1_sraa, SuperIRdecoder_1_mv, SuperIRdecoder_1_li, SuperIRdecoder_1_nott, wasload);

  // Notes on the sheet:
  //   wrote to rd
endmodule

module reliesonLoadchecker (
  input  [20:0] ID2EXir,
  input  [20:0] IF2IDir,
  output stall
);

  wire and_1_out, and_2_out, comparator_1_eq, comparator_2_eq, opcodeNeedsRS1check_1_needsrs1,
       opcodeNeedsRS2check_1_needsrs2, writestoRDcheck_1_wasload;
  wire [4:0] IRsplitter_1_rd, IRsplitter_2_rs1, IRsplitter_2_rs2;
  wire [5:0] IRsplitter_1_opcode, IRsplitter_2_opcode;

  IRsplitter IRsplitter_2 (
    .IR(IF2IDir), .rs2(IRsplitter_2_rs2), .opcode(IRsplitter_2_opcode), .rs1(IRsplitter_2_rs1));  // open: rd
  IRsplitter IRsplitter_1 (.IR(ID2EXir), .rd(IRsplitter_1_rd), .opcode(IRsplitter_1_opcode));  // open: rs2, rs1
  Comparator #(.width(5)) comparator_1 (
    .a(IRsplitter_1_rd), .b(IRsplitter_2_rs1), .eq(comparator_1_eq));  // open: gt, lt
  Comparator #(.width(5)) comparator_2 (
    .a(IRsplitter_1_rd), .b(IRsplitter_2_rs2), .eq(comparator_2_eq));  // open: gt, lt
  writestoRDcheck writestoRDcheck_1 (.op(IRsplitter_1_opcode), .wasload(writestoRDcheck_1_wasload));  // open: wrote
  opcodeNeedsRS1check opcodeNeedsRS1check_1 (.opcode(IRsplitter_2_opcode), .needsrs1(opcodeNeedsRS1check_1_needsrs1));
  opcodeNeedsRS2check opcodeNeedsRS2check_1 (.op(IRsplitter_2_opcode), .needsrs2(opcodeNeedsRS2check_1_needsrs2));
  and and_1 (and_1_out, opcodeNeedsRS1check_1_needsrs1, writestoRDcheck_1_wasload, comparator_1_eq);
  and and_2 (and_2_out, opcodeNeedsRS2check_1_needsrs2, writestoRDcheck_1_wasload, comparator_2_eq);
  or or_1 (stall, and_1_out, and_2_out);
endmodule

module opcodeNeedsRS1check (
  input  [5:0] opcode,
  output needsrs1
);

  wire SuperIRdecoder_1_add, SuperIRdecoder_1_adi, SuperIRdecoder_1_andd, SuperIRdecoder_1_andi,
       SuperIRdecoder_1_beq, SuperIRdecoder_1_bge, SuperIRdecoder_1_bgt, SuperIRdecoder_1_ble,
       SuperIRdecoder_1_blt, SuperIRdecoder_1_bne, SuperIRdecoder_1_jr, SuperIRdecoder_1_lw,
       SuperIRdecoder_1_mv, SuperIRdecoder_1_neg, SuperIRdecoder_1_nott, SuperIRdecoder_1_ori,
       SuperIRdecoder_1_orr, SuperIRdecoder_1_slli, SuperIRdecoder_1_slll, SuperIRdecoder_1_sraa,
       SuperIRdecoder_1_srai, SuperIRdecoder_1_srli, SuperIRdecoder_1_srll, SuperIRdecoder_1_sub,
       SuperIRdecoder_1_sw;

  SuperIRdecoder SuperIRdecoder_1 (
    .opcode(opcode), .sub(SuperIRdecoder_1_sub), .andi(SuperIRdecoder_1_andi), .ori(SuperIRdecoder_1_ori),
    .slli(SuperIRdecoder_1_slli), .srli(SuperIRdecoder_1_srli), .srai(SuperIRdecoder_1_srai),
    .beq(SuperIRdecoder_1_beq), .blt(SuperIRdecoder_1_blt), .bge(SuperIRdecoder_1_bge),
    .lw(SuperIRdecoder_1_lw), .sw(SuperIRdecoder_1_sw), .adi(SuperIRdecoder_1_adi),
    .add(SuperIRdecoder_1_add), .neg(SuperIRdecoder_1_neg), .andd(SuperIRdecoder_1_andd),
    .orr(SuperIRdecoder_1_orr), .slll(SuperIRdecoder_1_slll), .srll(SuperIRdecoder_1_srll),
    .sraa(SuperIRdecoder_1_sraa), .bne(SuperIRdecoder_1_bne), .bgt(SuperIRdecoder_1_bgt),
    .ble(SuperIRdecoder_1_ble), .jr(SuperIRdecoder_1_jr), .nott(SuperIRdecoder_1_nott),
    .mv(SuperIRdecoder_1_mv));  // open: j, jalr, nop, li, jal
  or or_1 (needsrs1, SuperIRdecoder_1_mv, SuperIRdecoder_1_sw, SuperIRdecoder_1_adi, SuperIRdecoder_1_add, SuperIRdecoder_1_sub, SuperIRdecoder_1_neg, SuperIRdecoder_1_andi, SuperIRdecoder_1_andd, SuperIRdecoder_1_ori, SuperIRdecoder_1_orr, SuperIRdecoder_1_slli, SuperIRdecoder_1_slll, SuperIRdecoder_1_srli, SuperIRdecoder_1_srll, SuperIRdecoder_1_srai, SuperIRdecoder_1_sraa, SuperIRdecoder_1_beq, SuperIRdecoder_1_bne, SuperIRdecoder_1_blt, SuperIRdecoder_1_bgt, SuperIRdecoder_1_bge, SuperIRdecoder_1_ble, SuperIRdecoder_1_lw, SuperIRdecoder_1_jr, SuperIRdecoder_1_nott);

  // Notes on the sheet:
  //   needs rs1
endmodule

module opcodeNeedsRS2check (
  input  [5:0] op,
  output needsrs2
);

  wire SuperIRdecoder_1_add, SuperIRdecoder_1_andd, SuperIRdecoder_1_beq, SuperIRdecoder_1_bge,
       SuperIRdecoder_1_bgt, SuperIRdecoder_1_ble, SuperIRdecoder_1_blt, SuperIRdecoder_1_bne,
       SuperIRdecoder_1_neg, SuperIRdecoder_1_orr, SuperIRdecoder_1_slll, SuperIRdecoder_1_sraa,
       SuperIRdecoder_1_srll, SuperIRdecoder_1_sub, SuperIRdecoder_1_sw;

  SuperIRdecoder SuperIRdecoder_1 (
    .opcode(op), .sub(SuperIRdecoder_1_sub), .beq(SuperIRdecoder_1_beq), .blt(SuperIRdecoder_1_blt),
    .bge(SuperIRdecoder_1_bge), .sw(SuperIRdecoder_1_sw), .add(SuperIRdecoder_1_add),
    .neg(SuperIRdecoder_1_neg), .andd(SuperIRdecoder_1_andd), .orr(SuperIRdecoder_1_orr),
    .slll(SuperIRdecoder_1_slll), .srll(SuperIRdecoder_1_srll), .sraa(SuperIRdecoder_1_sraa),
    .bne(SuperIRdecoder_1_bne), .bgt(SuperIRdecoder_1_bgt), .ble(SuperIRdecoder_1_ble));  // open: andi, ori, slli, srli, srai, j, lw, jalr, nop, li, adi, jal, jr, nott, mv
  or or_1 (needsrs2, SuperIRdecoder_1_sw, SuperIRdecoder_1_add, SuperIRdecoder_1_sub, SuperIRdecoder_1_neg, SuperIRdecoder_1_andd, SuperIRdecoder_1_orr, SuperIRdecoder_1_slll, SuperIRdecoder_1_srll, SuperIRdecoder_1_sraa, SuperIRdecoder_1_beq, SuperIRdecoder_1_bne, SuperIRdecoder_1_blt, SuperIRdecoder_1_bgt, SuperIRdecoder_1_bge, SuperIRdecoder_1_ble);

  // Notes on the sheet:
  //   needs rs2
endmodule

module IRNormalizer (
  input  [31:0] IR,
  output [20:0] normIR,
  output [31:0] signextendIMM
);

  wire or_1_out, or_2_out, or_3_out, or_4_out, superirdecoder_1_add, superirdecoder_1_adi,
       superirdecoder_1_andd, superirdecoder_1_andi, superirdecoder_1_beq, superirdecoder_1_bge,
       superirdecoder_1_bgt, superirdecoder_1_ble, superirdecoder_1_blt, superirdecoder_1_bne,
       superirdecoder_1_j, superirdecoder_1_jr, superirdecoder_1_li, superirdecoder_1_lw,
       superirdecoder_1_mv, superirdecoder_1_neg, superirdecoder_1_nop, superirdecoder_1_nott,
       superirdecoder_1_ori, superirdecoder_1_orr, superirdecoder_1_slli, superirdecoder_1_slll,
       superirdecoder_1_sraa, superirdecoder_1_srai, superirdecoder_1_srli, superirdecoder_1_srll,
       superirdecoder_1_sub, superirdecoder_1_sw;
  wire [1:0] priority_encoder_1_out;
  wire [31:0] bit_extender_1_out, bit_extender_2_out, bit_extender_3_out, bit_extender_4_out;

  SuperIRdecoder superirdecoder_1 (
    .opcode(IR[5:0]), .sub(superirdecoder_1_sub), .andi(superirdecoder_1_andi), .ori(superirdecoder_1_ori),
    .slli(superirdecoder_1_slli), .srli(superirdecoder_1_srli), .srai(superirdecoder_1_srai),
    .j(superirdecoder_1_j), .beq(superirdecoder_1_beq), .blt(superirdecoder_1_blt),
    .bge(superirdecoder_1_bge), .lw(superirdecoder_1_lw), .nop(superirdecoder_1_nop),
    .sw(superirdecoder_1_sw), .li(superirdecoder_1_li), .adi(superirdecoder_1_adi),
    .add(superirdecoder_1_add), .neg(superirdecoder_1_neg), .andd(superirdecoder_1_andd),
    .orr(superirdecoder_1_orr), .slll(superirdecoder_1_slll), .srll(superirdecoder_1_srll),
    .sraa(superirdecoder_1_sraa), .bne(superirdecoder_1_bne), .bgt(superirdecoder_1_bgt),
    .ble(superirdecoder_1_ble), .jr(superirdecoder_1_jr), .nott(superirdecoder_1_nott),
    .mv(superirdecoder_1_mv));  // open: jalr, jal
  assign bit_extender_1_out = {{11{IR[31]}}, IR[31:11]};  // Bit_Extender bit_extender_1
  assign bit_extender_2_out = {{16{IR[31]}}, IR[31:16]};  // Bit_Extender bit_extender_2
  assign bit_extender_3_out = {{16{IR[31]}}, IR[31:16]};  // Bit_Extender bit_extender_3
  assign bit_extender_4_out = {{21{IR[31]}}, IR[31:21]};  // Bit_Extender bit_extender_4
  or or_1 (or_1_out, superirdecoder_1_li, superirdecoder_1_nop, superirdecoder_1_j);
  or or_2 (or_2_out, superirdecoder_1_sw, superirdecoder_1_beq, superirdecoder_1_bne, superirdecoder_1_blt, superirdecoder_1_bgt, superirdecoder_1_bge, superirdecoder_1_ble);
  or or_3 (or_3_out, superirdecoder_1_adi, superirdecoder_1_neg, superirdecoder_1_andi, superirdecoder_1_ori, superirdecoder_1_slli, superirdecoder_1_srli, superirdecoder_1_srai, superirdecoder_1_lw, superirdecoder_1_jr, superirdecoder_1_nott, superirdecoder_1_mv);
  or or_4 (or_4_out, superirdecoder_1_add, superirdecoder_1_sub, superirdecoder_1_andd, superirdecoder_1_orr, superirdecoder_1_slll, superirdecoder_1_srll, superirdecoder_1_sraa);
  Priority_Encoder #(.select(2)) priority_encoder_1 (
    .in0(or_1_out), .in1(or_2_out), .in2(or_3_out), .in3(or_4_out), .out(priority_encoder_1_out));  // open: gs, en_out, en_in
  Multiplexer #(.select(2), .width(21)) multiplexer_1 (
    .in0({IR[10:6], {10{1'b0}}, IR[5:0]}), .in1({{5{1'b0}}, IR[15:0]}),
    .in2({IR[10:6], IR[15:11], {5{1'b0}}, IR[5:0]}), .in3(IR[20:0]), .out(normIR),
    .sel(priority_encoder_1_out));
  Multiplexer #(.select(2), .width(32)) multiplexer_2 (
    .in0(bit_extender_1_out), .in1(bit_extender_2_out), .in2(bit_extender_3_out), .in3(bit_extender_4_out),
    .out(signextendIMM), .sel(priority_encoder_1_out));

  // Notes on the sheet:
  //   IMM_RD
  //   IMM_RS1_RS2
  //   IMM_RS1_RD
  //   op
  //   rs2
  //   rs1
  //   rd
  //   IMM_RD_RS1_RS2
  //   IMM_RD
  //   IMM_RS1_RS2
  //   IMM_RS1_RD
  //   IMM_RD_RS1_RS2
  //   RD_RS1_RS2_OP
endmodule

module memMappedIO (
  input  [31:0] data,
  input  [20:0] IR,
  input  [31:0] addr,
  output [4:0] screenx,
  output [4:0] screeny,
  output [14:0] screencolor,
  output screenWE
);

  wire comparator_1_eq, memreadorwrite_1_we;

  memreadorwrite memreadorwrite_1 (.IR(IR), .WE(memreadorwrite_1_we));  // open: OE
  Comparator #(.width(32)) comparator_1 (.a(32'h7531), .b(addr), .eq(comparator_1_eq));  // open: gt, lt
  and and_1 (screenWE, memreadorwrite_1_we, comparator_1_eq);

  assign screencolor = data[24:10];
  assign screenx = data[4:0];
  assign screeny = data[9:5];
endmodule
